// Logisim project CRC.circ as structural Verilog: 2 circuits, main circuit mod2
module CRC (
  input  [7:0] A,
  input  [3:0] B,
  output [10:0] C
);

  wire [2:0] mod2_1_c, mod2_2_c, mod2_3_c, mod2_4_c, mod2_5_c, mod2_6_c, mod2_7_c, shifter_1_out;
  wire [10:0] bit_extender_1_out;

  assign bit_extender_1_out = {{3{1'b0}}, A};  // Bit_Extender bit_extender_1
  mod2 mod2_1 (.A(C[10:7]), .B(B), .C(mod2_1_c));  // open: D
  // Probe on {C[10:3], shifter_1_out}
  Shifter #(.width(11)) shifter_1 (.in(bit_extender_1_out), .\dist (4'b0011), .out({C[10:3], shifter_1_out}));
  mod2 mod2_2 (.A({mod2_1_c, C[6]}), .B(B), .C(mod2_2_c));  // open: D
  mod2 mod2_3 (.A({mod2_2_c, C[5]}), .B(B), .C(mod2_3_c));  // open: D
  mod2 mod2_4 (.A({mod2_3_c, C[4]}), .B(B), .C(mod2_4_c));  // open: D
  mod2 mod2_5 (.A({mod2_4_c, C[3]}), .B(B), .C(mod2_5_c));  // open: D
  mod2 mod2_6 (.A({mod2_5_c, shifter_1_out[2]}), .B(B), .C(mod2_6_c));  // open: D
  mod2 mod2_7 (.A({mod2_6_c, shifter_1_out[1]}), .B(B), .C(mod2_7_c));  // open: D
  // Probe on C[2:0]
  mod2 mod2_8 (.A({mod2_7_c, shifter_1_out[0]}), .B(B), .C(C[2:0]));  // open: D

  // Other names for the same wires on the sheet: 余数[2:0] = C[2:0]; _1[3:0] = C[10:7]; 除数[3:0] = B
endmodule

module mod2 (
  input  [3:0] A,
  input  [3:0] B,
  output [2:0] C,
  output D
);

  wire [3:0] xor_1_out;

  and and_1 (D, A[3], 1'b1);
  assign xor_1_out = B ^ A;  // XOR_Gate xor_1, 4 bits wide
  Multiplexer #(.width(3)) multiplexer_1 (.in0(A[2:0]), .in1(xor_1_out[2:0]), .out(C), .sel(D));  // open: en
endmodule
