// Logisim project P0-3.circ as structural Verilog: 3 circuits, main circuit main
module main (
  input  [3:0] from,
  input  [7:0] num0,
  input  [7:0] num1,
  input  [7:0] num2,
  input  [7:0] num3,
  output [7:0] \output 
);

  wire comparator_1_lt, comparator_2_lt, comparator_3_lt, comparator_4_lt, comparator_5_lt, comparator_6_lt,
       isa, isb, isc, isd, subtractor_1_bout, subtractor_2_bout, subtractor_3_bout;
  wire [3:0] comparator_7_eq, comparator_11_eq, comparator_15_eq;
  wire [7:0] A, A1, A2, A3, adder_1_out, B, B1, B2, B3, C, C1, C2, C3, cur_floor1, cur_floor2, cur_floor3, D,
       D1, D2, D3, distance1, distance2, distance3, first_floor, negator_1_out, negator_2_out, negator_3_out,
       subtractor_1_out, subtractor_2_out, subtractor_3_out;

  Decoder #(.select(4)) decoder_1 (
    .out1(isa), .out2(isb), .out4(isc), .out8(isd), .sel(from));  // open: out0, out3, out5, out6, out7, out9, out10, out11, out12, out13, out14, out15, en
  Multiplexer #(.select(4), .width(8)) multiplexer_1 (
    .in1({8{1'b0}}), .in2(8'h1), .in4(8'h2), .in8(8'h3), .out(first_floor), .sel({isd, isc, isb, isa}));  // open: in0, in3, in5, in6, in7, in9, in10, in11, in12, in13, in14, in15, en
  Comparator #(.mode("unsigned")) comparator_1 (.a(A), .b(B), .lt(comparator_1_lt));  // open: gt, eq
  Comparator #(.mode("unsigned")) comparator_2 (.a(A1), .b(C), .lt(comparator_2_lt));  // open: gt, eq
  Comparator #(.mode("unsigned")) comparator_3 (.a(A2), .b(D), .lt(comparator_3_lt));  // open: gt, eq
  Comparator #(.mode("unsigned")) comparator_4 (.a(B1), .b(C1), .lt(comparator_4_lt));  // open: gt, eq
  Comparator #(.mode("unsigned")) comparator_5 (.a(B2), .b(D1), .lt(comparator_5_lt));  // open: gt, eq
  Comparator #(.mode("unsigned")) comparator_6 (.a(C2), .b(D2), .lt(comparator_6_lt));  // open: gt, eq
  // Probe on first_floor
  _8bit_swap u_8bit_swap_1 (.in1(A), .in2(B), .s(comparator_1_lt), .o1(A1), .o2(B1));
  _8bit_swap u_8bit_swap_2 (.in1(A1), .in2(C), .s(comparator_2_lt), .o1(A2), .o2(C1));
  _8bit_swap u_8bit_swap_3 (.in1(A2), .in2(D), .s(comparator_3_lt), .o1(A3), .o2(D1));
  _8bit_swap u_8bit_swap_4 (.in1(B1), .in2(C1), .s(comparator_4_lt), .o1(B2), .o2(C2));
  _8bit_swap u_8bit_swap_5 (.in1(B2), .in2(D1), .s(comparator_5_lt), .o1(B3), .o2(D2));
  _8bit_swap u_8bit_swap_6 (.in1(C2), .in2(D2), .s(comparator_6_lt), .o1(C3), .o2(D3));
  Multiplexer #(.width(8)) multiplexer_2 (.in0(num0), .in1({8{1'b0}}), .out(A), .sel(isa));  // open: en
  // Probe on A3
  // Probe on B3
  // Probe on D3
  Multiplexer #(.width(8)) multiplexer_3 (.in0(num1), .in1({8{1'b0}}), .out(B), .sel(isb));  // open: en
  // Probe on C3
  Multiplexer #(.width(8)) multiplexer_4 (.in0(num2), .in1({8{1'b0}}), .out(C), .sel(isc));  // open: en
  Comparator #(.mode("unsigned")) comparator_7 (.a(num0), .b(A3), .eq(comparator_7_eq[0]));  // open: gt, lt
  Comparator #(.mode("unsigned")) comparator_8 (.a(num1), .b(A3), .eq(comparator_7_eq[1]));  // open: gt, lt
  Comparator #(.mode("unsigned")) comparator_9 (.a(num2), .b(A3), .eq(comparator_7_eq[2]));  // open: gt, lt
  Comparator #(.mode("unsigned")) comparator_10 (.a(num3), .b(A3), .eq(comparator_7_eq[3]));  // open: gt, lt
  Comparator #(.mode("unsigned")) comparator_11 (.a(num0), .b(B3), .eq(comparator_11_eq[0]));  // open: gt, lt
  Comparator #(.mode("unsigned")) comparator_12 (.a(num1), .b(B3), .eq(comparator_11_eq[1]));  // open: gt, lt
  Comparator #(.mode("unsigned")) comparator_13 (.a(num2), .b(B3), .eq(comparator_11_eq[2]));  // open: gt, lt
  Comparator #(.mode("unsigned")) comparator_14 (.a(num3), .b(B3), .eq(comparator_11_eq[3]));  // open: gt, lt
  Comparator #(.mode("unsigned")) comparator_15 (.a(num0), .b(C3), .eq(comparator_15_eq[0]));  // open: gt, lt
  Comparator #(.mode("unsigned")) comparator_16 (.a(num1), .b(C3), .eq(comparator_15_eq[1]));  // open: gt, lt
  Comparator #(.mode("unsigned")) comparator_17 (.a(num2), .b(C3), .eq(comparator_15_eq[2]));  // open: gt, lt
  Comparator #(.mode("unsigned")) comparator_18 (.a(num3), .b(C3), .eq(comparator_15_eq[3]));  // open: gt, lt
  // Probe on comparator_7_eq
  Multiplexer #(.width(8)) multiplexer_5 (.in0(num3), .in1({8{1'b0}}), .out(D), .sel(isd));  // open: en
  Multiplexer #(.select(4), .width(8)) multiplexer_6 (
    .in1({8{1'b0}}), .in2(8'h1), .in4(8'h2), .in8(8'h3), .out(cur_floor1), .sel(comparator_7_eq));  // open: in0, in3, in5, in6, in7, in9, in10, in11, in12, in13, in14, in15, en
  Multiplexer #(.select(4), .width(8)) multiplexer_7 (
    .in1({8{1'b0}}), .in2(8'h1), .in4(8'h2), .in8(8'h3), .out(cur_floor2), .sel(comparator_11_eq));  // open: in0, in3, in5, in6, in7, in9, in10, in11, in12, in13, in14, in15, en
  Multiplexer #(.select(4), .width(8)) multiplexer_8 (
    .in1({8{1'b0}}), .in2(8'h1), .in4(8'h2), .in8(8'h3), .out(cur_floor3), .sel(comparator_15_eq));  // open: in0, in3, in5, in6, in7, in9, in10, in11, in12, in13, in14, in15, en
  // Probe on cur_floor2
  // Probe on cur_floor3
  // Probe on cur_floor1
  Subtractor subtractor_1 (
    .a(cur_floor1), .b(first_floor), .out(subtractor_1_out), .bout(subtractor_1_bout));  // open: bin
  Subtractor subtractor_2 (
    .a(cur_floor2), .b(cur_floor1), .out(subtractor_2_out), .bout(subtractor_2_bout));  // open: bin
  Negator negator_1 (.in(subtractor_2_out), .out(negator_1_out));
  Subtractor subtractor_3 (
    .a(cur_floor3), .b(cur_floor2), .out(subtractor_3_out), .bout(subtractor_3_bout));  // open: bin
  // Probe on distance1
  Multiplexer #(.width(8)) multiplexer_9 (
    .in0(subtractor_1_out), .in1(negator_2_out), .out(distance1), .sel(subtractor_1_bout));  // open: en
  Negator negator_2 (.in(subtractor_1_out), .out(negator_2_out));
  Multiplexer #(.width(8)) multiplexer_10 (
    .in0(subtractor_2_out), .in1(negator_1_out), .out(distance2), .sel(subtractor_2_bout));  // open: en
  Multiplexer #(.width(8)) multiplexer_11 (
    .in0(subtractor_3_out), .in1(negator_3_out), .out(distance3), .sel(subtractor_3_bout));  // open: en
  Negator negator_3 (.in(subtractor_3_out), .out(negator_3_out));
  // Probe on distance2
  // Probe on distance3
  Adder adder_1 (.a(distance1), .b(distance2), .out(adder_1_out));  // open: cin, cout
  Adder adder_2 (.a(adder_1_out), .b(distance3), .out(\output ));  // open: cin, cout

  // Other names for the same wires on the sheet: a_t[7:0] = num0; b_t[7:0] = num1; c_t[7:0] = num2; d_t[7:0] = num3
endmodule

module _1bit_swap (
  input  in1,
  input  in2,
  input  s,
  output o1,
  output o2
);

  wire and_1_out, and_2_out, and_3_out, and_4_out, not_1_out, not_2_out;

  not not_1 (not_1_out, s);
  not not_2 (not_2_out, s);
  and and_1 (and_1_out, in2, s);
  and and_2 (and_2_out, in1, not_1_out);
  and and_3 (and_3_out, in2, not_2_out);
  and and_4 (and_4_out, in1, s);
  or or_1 (o1, and_1_out, and_2_out);
  or or_2 (o2, and_3_out, and_4_out);
endmodule

module _8bit_swap (
  input  [7:0] in1,
  input  [7:0] in2,
  input  s,
  output [7:0] o1,
  output [7:0] o2
);

  _1bit_swap u_1bit_swap_1 (.in1(in1[0]), .in2(in2[0]), .s(s), .o1(o1[0]), .o2(o2[0]));
  _1bit_swap u_1bit_swap_2 (.in1(in1[1]), .in2(in2[1]), .s(s), .o1(o1[1]), .o2(o2[1]));
  _1bit_swap u_1bit_swap_3 (.in1(in1[2]), .in2(in2[2]), .s(s), .o1(o1[2]), .o2(o2[2]));
  _1bit_swap u_1bit_swap_4 (.in1(in1[3]), .in2(in2[3]), .s(s), .o1(o1[3]), .o2(o2[3]));
  _1bit_swap u_1bit_swap_5 (.in1(in1[4]), .in2(in2[4]), .s(s), .o1(o1[4]), .o2(o2[4]));
  _1bit_swap u_1bit_swap_6 (.in1(in1[5]), .in2(in2[5]), .s(s), .o1(o1[5]), .o2(o2[5]));
  _1bit_swap u_1bit_swap_7 (.in1(in1[6]), .in2(in2[6]), .s(s), .o1(o1[6]), .o2(o2[6]));
  _1bit_swap u_1bit_swap_8 (.in1(in1[7]), .in2(in2[7]), .s(s), .o1(o1[7]), .o2(o2[7]));
endmodule
