// Logisim project CPU.circ as structural Verilog: 11 circuits, main circuit main
module main (
  input  reset,
  output [31:0] out_2,
  output [31:0] out_3,
  output out_4,
  output [4:0] out_5,
  output [31:0] out_6,
  output out_7,
  output [31:0] out_8,
  output [31:0] out_9
);

  wire ALUIBSel, clk, DMtoGRFSel, EXTType, GRF_A3Sel, PC_4toGRFSel, raSel, zero;
  wire [1:0] LoadTypeSel, NPCSel, StoreTypeSel;
  wire [4:0] ALUSel, multiplexer_1_out;
  wire [31:0] dm_1_data, GRF, grf_1_rd2, imm32, loadtype_1_out_4, multiplexer_2_out, multiplexer_5_out,
       npc_1_npc, PC_4;

  Clock u_clk (.out(clk));
  Multiplexer #(.width(5)) multiplexer_1 (
    .in0(out_2[20:16]), .in1(out_2[15:11]), .out(multiplexer_1_out), .sel(GRF_A3Sel));  // open: en
  NPC npc_1 (
    .PC(out_3), .imm26(out_2[25:0]), .GRF(GRF), .imm16(out_2[15:0]), .NPCSel(NPCSel), .zero(zero),
    .NPC(npc_1_npc), .PC_4(PC_4));
  Multiplexer #(.width(32)) multiplexer_2 (
    .in0(out_8), .in1(loadtype_1_out_4), .out(multiplexer_2_out), .sel(DMtoGRFSel));  // open: en
  PC pc_1 (.clk(clk), .reset(reset), .NPC(npc_1_npc), .PC(out_3));
  Multiplexer #(.width(5)) multiplexer_3 (
    .in0(multiplexer_1_out), .in1({5{1'b1}}), .out(out_5), .sel(raSel));  // open: en
  Multiplexer #(.width(32)) multiplexer_4 (
    .in0(multiplexer_2_out), .in1(PC_4), .out(out_6), .sel(PC_4toGRFSel));  // open: en
  IM im_1 (.Addr(out_3), .Instr(out_2));
  GRF grf_1 (
    .clk(clk), .reset(reset), .WE(out_4), .A1(out_2[25:21]), .A2(out_2[20:16]), .A3(out_5), .WD(out_6),
    .RD1(GRF), .RD2(grf_1_rd2));
  Multiplexer #(.width(32)) multiplexer_5 (
    .in0(grf_1_rd2), .in1(imm32), .out(multiplexer_5_out), .sel(ALUIBSel));  // open: en
  ALU alu_1 (.A(GRF), .B(multiplexer_5_out), .sll(out_2[10:6]), .ALUSel(ALUSel), .\output (out_8), .zero(zero));
  EXT ext_1 (.imm16(out_2[15:0]), .sel(EXTType), .imm32(imm32));
  Controller controller_1 (
    .Opcode(out_2[31:26]), .funct(out_2[5:0]), .NPCSel(NPCSel), .GRFEnable(out_4), .EXTType(EXTType),
    .Type(ALUSel), .ALUIBSel(ALUIBSel), .GRF_A3Sel(GRF_A3Sel), .DMEnable(out_7), .DMtoGRFSel(DMtoGRFSel),
    .PC_4toGRFSel(PC_4toGRFSel), .raSel(raSel), .StoreType(StoreTypeSel), .LoadType(LoadTypeSel));
  StoreType storetype_1 (.Src(loadtype_1_out_4), .Data(grf_1_rd2), .Addr(out_8), .TypeSel(StoreTypeSel), .out_5(out_9));
  DM dm_1 (.clk(clk), .reset(reset), .WE(out_7), .Addr(out_8), .WD(out_9), .Data(dm_1_data));
  LoadType loadtype_1 (.Data(dm_1_data), .Addr(out_8), .TypeSel(LoadTypeSel), .out_4(loadtype_1_out_4));

  // Other names for the same wires on the sheet: DMEnable = out_7; GRFEnable = out_4; funct[5:0] = out_2[5:0];
  //   imm16[15:0] = out_2[15:0]; imm26[25:0] = out_2[25:0]; Instr[31:0] = out_2; shamt[4:0] = out_2[10:6];
  //   rd[4:0] = out_2[15:11]; rt[4:0] = out_2[20:16]; rs[4:0] = out_2[25:21]; Opcode[5:0] = out_2[31:26];
  //   MemAddr[31:0] = out_8; MemData[31:0] = out_9; PC[31:0] = out_3; RegAddr[4:0] = out_5; RegData[31:0] = out_6;
  //   rst = reset

  // Notes on the sheet:
  //   PC+4，jal 等
  //   先选目标是否是$ra，再选rt或rd
  //   先选是否PC+4，再选是否来自DM
  //   IFU
  //   F级
  //   D级0
  //   Data calculated by ALU
  //   Data from DM
  //   rs
  //   rt
  //   imm32 from imm16
  //   rt 是将要存入 DM 的数据
  //   E级1
  //   use result as address
  //   M级2
  //   address
  //   W级3
  //   RegWrite
  //   MemWrite
endmodule

module PC (
  input  clk,
  input  reset,
  input  [31:0] NPC,
  output [31:0] PC
);

  wire counter_1_carry;
  wire [31:0] register_1_q;

  Register #(.width(32)) register_1 (.D(NPC), .Q(register_1_q), .clk(clk), .clr(reset));  // open: en
  Counter #(.width(1), .max('h1), .ongoal("stay")) counter_1 (
    .carry(counter_1_carry), .clk(clk), .clr(reset));  // open: load, D, count, Q
  Multiplexer #(.width(32)) multiplexer_1 (
    .in0(32'h3000), .in1(register_1_q), .out(PC), .sel(counter_1_carry));  // open: en

  // Other names for the same wires on the sheet: rst = reset
endmodule

module NPC (
  input  [31:0] PC,
  input  [25:0] imm26,
  input  [31:0] GRF,
  input  [15:0] imm16,
  input  [1:0] NPCSel,
  input  zero,
  output [31:0] PC_4,
  output [31:0] NPC
);

  wire [31:0] adder_2_out, bit_extender_1_out, multiplexer_1_out;

  Adder #(.width(32)) adder_1 (.a(PC), .b(32'h4), .out(PC_4));  // open: cin, cout
  assign bit_extender_1_out = {{14{imm16[15]}}, {imm16, 2'b00}};  // Bit_Extender bit_extender_1
  Adder #(.width(32)) adder_2 (.a(PC_4), .b(bit_extender_1_out), .out(adder_2_out));  // open: cin, cout
  Multiplexer #(.width(32)) multiplexer_1 (
    .in0(PC_4), .in1(adder_2_out), .out(multiplexer_1_out), .sel(zero));  // open: en
  Multiplexer #(.select(2), .width(32)) multiplexer_2 (
    .in0(PC_4), .in1({PC[31:28], imm26, 2'b00}), .in2(GRF), .in3(multiplexer_1_out), .out(NPC), .sel(NPCSel));  // open: en

  // Notes on the sheet:
  //   Instr_Index
  //   offset
  //   imm26 || 00
  //   offset || 00
  //   PC[31:28]
  //   例如jr
  //   PC + 4
  //   beq类，条件判断成功则 zero 为 1
endmodule

module IM (
  input  [31:0] Addr,
  output [31:0] Instr
);

  wire [31:0] shifter_1_out, subtractor_1_out;

  // Probe on subtractor_1_out
  Subtractor #(.width(32)) subtractor_1 (.a(Addr), .b(32'h3000), .out(subtractor_1_out));  // open: bin, bout
  // Probe on shifter_1_out[11:0]
  Shifter #(.width(32), .shift("lr")) shifter_1 (.in(subtractor_1_out), .\dist (5'b00010), .out(shifter_1_out));
  ROM #(.addrWidth(12), .dataWidth(32)) rom_1 (.addr(shifter_1_out[11:0]), .data(Instr));  // open: sel

  // Notes on the sheet:
  //   PC值
  //   (PC -0x00003000) / 4 映射到指令序号
  //   低 12 位
  //   Instr_Mem  4096*32 bit
  //   contents of rom_1 (hex, n*v repeats v):
  //   3c011234 34285678 a0080001 a0080003 80090003 800a0001
endmodule

module GRF (
  input  clk,
  input  reset,
  input  WE,
  input  [4:0] A1,
  input  [4:0] A2,
  input  [4:0] A3,
  input  [31:0] WD,
  output [31:0] RD1,
  output [31:0] RD2
);

  wire is2, is3, is4, is5, is6, is7, is8, is9, is10, is11, is12, is13, is14, is15, is16, is17, is18, is19,
       is20, is21, is22, is23, is24, is25, is26, is27, is28, is29, is30, is31, is32;
  wire [31:0] _1, _1_prime, _2, _2_prime, _3, _3_prime, _4, _4_prime, _5, _5_prime, _6, _6_prime, _7,
       _7_prime, _8, _8_prime, _9, _9_prime, _10, _10_prime, _11, _11_prime, _12, _12_prime, _13, _13_prime,
       _14, _14_prime, _15, _15_prime, _16, _16_prime, _17, _17_prime, _18, _18_prime, _19, _19_prime, _20,
       _20_prime, _21, _21_prime, _22, _22_prime, _23, _23_prime, _24, _24_prime, _25, _25_prime, _26,
       _26_prime, _27, _27_prime, _28, _28_prime, _29, _29_prime, _30, _30_prime, _31, _31_prime, _32,
       _32_prime;

  Comparator #(.width(5), .mode("unsigned")) comparator_1 (.a(A3), .b(5'b00001), .eq(is2));  // open: gt, lt
  Comparator #(.width(5), .mode("unsigned")) comparator_2 (.a(A3), .b(5'b00010), .eq(is3));  // open: gt, lt
  Comparator #(.width(5), .mode("unsigned")) comparator_3 (.a(A3), .b(5'b00011), .eq(is4));  // open: gt, lt
  Comparator #(.width(5), .mode("unsigned")) comparator_4 (.a(A3), .b(5'b00100), .eq(is5));  // open: gt, lt
  Comparator #(.width(5), .mode("unsigned")) comparator_5 (.a(A3), .b(5'b00101), .eq(is6));  // open: gt, lt
  Comparator #(.width(5), .mode("unsigned")) comparator_6 (.a(A3), .b(5'b00110), .eq(is7));  // open: gt, lt
  Comparator #(.width(5), .mode("unsigned")) comparator_7 (.a(A3), .b(5'b00111), .eq(is8));  // open: gt, lt
  Comparator #(.width(5), .mode("unsigned")) comparator_8 (.a(A3), .b(5'b01000), .eq(is9));  // open: gt, lt
  Comparator #(.width(5), .mode("unsigned")) comparator_9 (.a(A3), .b(5'b01001), .eq(is10));  // open: gt, lt
  Comparator #(.width(5), .mode("unsigned")) comparator_10 (.a(A3), .b(5'b01010), .eq(is11));  // open: gt, lt
  Comparator #(.width(5), .mode("unsigned")) comparator_11 (.a(A3), .b(5'b01011), .eq(is12));  // open: gt, lt
  Comparator #(.width(5), .mode("unsigned")) comparator_12 (.a(A3), .b(5'b01100), .eq(is13));  // open: gt, lt
  Comparator #(.width(5), .mode("unsigned")) comparator_13 (.a(A3), .b(5'b01101), .eq(is14));  // open: gt, lt
  Comparator #(.width(5), .mode("unsigned")) comparator_14 (.a(A3), .b(5'b01110), .eq(is15));  // open: gt, lt
  Comparator #(.width(5), .mode("unsigned")) comparator_15 (.a(A3), .b(5'b01111), .eq(is16));  // open: gt, lt
  Comparator #(.width(5), .mode("unsigned")) comparator_16 (.a(A3), .b(5'b10000), .eq(is17));  // open: gt, lt
  Comparator #(.width(5), .mode("unsigned")) comparator_17 (.a(A3), .b(5'b10001), .eq(is18));  // open: gt, lt
  Comparator #(.width(5), .mode("unsigned")) comparator_18 (.a(A3), .b(5'b10010), .eq(is19));  // open: gt, lt
  Comparator #(.width(5), .mode("unsigned")) comparator_19 (.a(A3), .b(5'b10011), .eq(is20));  // open: gt, lt
  Comparator #(.width(5), .mode("unsigned")) comparator_20 (.a(A3), .b(5'b10100), .eq(is21));  // open: gt, lt
  Comparator #(.width(5), .mode("unsigned")) comparator_21 (.a(A3), .b(5'b10101), .eq(is22));  // open: gt, lt
  Comparator #(.width(5), .mode("unsigned")) comparator_22 (.a(A3), .b(5'b10110), .eq(is23));  // open: gt, lt
  Comparator #(.width(5), .mode("unsigned")) comparator_23 (.a(A3), .b(5'b10111), .eq(is24));  // open: gt, lt
  Comparator #(.width(5), .mode("unsigned")) comparator_24 (.a(A3), .b(5'b11000), .eq(is25));  // open: gt, lt
  Comparator #(.width(5), .mode("unsigned")) comparator_25 (.a(A3), .b(5'b11001), .eq(is26));  // open: gt, lt
  Comparator #(.width(5), .mode("unsigned")) comparator_26 (.a(A3), .b(5'b11010), .eq(is27));  // open: gt, lt
  Comparator #(.width(5), .mode("unsigned")) comparator_27 (.a(A3), .b(5'b11011), .eq(is28));  // open: gt, lt
  Comparator #(.width(5), .mode("unsigned")) comparator_28 (.a(A3), .b(5'b11100), .eq(is29));  // open: gt, lt
  Comparator #(.width(5), .mode("unsigned")) comparator_29 (.a(A3), .b(5'b11101), .eq(is30));  // open: gt, lt
  Comparator #(.width(5), .mode("unsigned")) comparator_30 (.a(A3), .b(5'b11110), .eq(is31));  // open: gt, lt
  Comparator #(.width(5), .mode("unsigned")) comparator_31 (.a(A3), .b({5{1'b1}}), .eq(is32));  // open: gt, lt
  // Probe on _1
  Demultiplexer #(.select(5), .width(32)) demultiplexer_1 (
    .out0(_1), .out1(_2), .out2(_3), .out3(_4), .out4(_5), .out5(_6), .out6(_7), .out7(_8), .out8(_9),
    .out9(_10), .out10(_11), .out11(_12), .out12(_13), .out13(_14), .out14(_15), .out15(_16), .out16(_17),
    .out17(_18), .out18(_19), .out19(_20), .out20(_21), .out21(_22), .out22(_23), .out23(_24), .out24(_25),
    .out25(_26), .out26(_27), .out27(_28), .out28(_29), .out29(_30), .out30(_31), .out31(_32), .in(WD),
    .sel(A3), .en(WE));
  Register #(.width(32)) register_1 (.D({32{1'b0}}), .Q(_1_prime), .clk(clk), .clr(reset));  // open: en
  Register #(.width(32)) register_2 (.D(_5), .en(is5), .Q(_5_prime), .clk(clk), .clr(reset));
  Register #(.width(32)) register_3 (.D(_9), .en(is9), .Q(_9_prime), .clk(clk), .clr(reset));
  Register #(.width(32)) register_4 (.D(_13), .en(is13), .Q(_13_prime), .clk(clk), .clr(reset));
  Register #(.width(32)) register_5 (.D(_17), .en(is17), .Q(_17_prime), .clk(clk), .clr(reset));
  Register #(.width(32)) register_6 (.D(_21), .en(is21), .Q(_21_prime), .clk(clk), .clr(reset));
  Register #(.width(32)) register_7 (.D(_25), .en(is25), .Q(_25_prime), .clk(clk), .clr(reset));
  Register #(.width(32)) register_8 (.D(_29), .en(is29), .Q(_29_prime), .clk(clk), .clr(reset));
  Register #(.width(32)) register_9 (.D(_2), .en(is2), .Q(_2_prime), .clk(clk), .clr(reset));
  Register #(.width(32)) register_10 (.D(_6), .en(is6), .Q(_6_prime), .clk(clk), .clr(reset));
  Register #(.width(32)) register_11 (.D(_10), .en(is10), .Q(_10_prime), .clk(clk), .clr(reset));
  Register #(.width(32)) register_12 (.D(_14), .en(is14), .Q(_14_prime), .clk(clk), .clr(reset));
  Register #(.width(32)) register_13 (.D(_18), .en(is18), .Q(_18_prime), .clk(clk), .clr(reset));
  Register #(.width(32)) register_14 (.D(_22), .en(is22), .Q(_22_prime), .clk(clk), .clr(reset));
  Register #(.width(32)) register_15 (.D(_26), .en(is26), .Q(_26_prime), .clk(clk), .clr(reset));
  Register #(.width(32)) register_16 (.D(_30), .en(is30), .Q(_30_prime), .clk(clk), .clr(reset));
  Multiplexer #(.select(5), .width(32)) multiplexer_1 (
    .in0(_1_prime), .in1(_2_prime), .in2(_3_prime), .in3(_4_prime), .in4(_5_prime), .in5(_6_prime),
    .in6(_7_prime), .in7(_8_prime), .in8(_9_prime), .in9(_10_prime), .in10(_11_prime), .in11(_12_prime),
    .in12(_13_prime), .in13(_14_prime), .in14(_15_prime), .in15(_16_prime), .in16(_17_prime),
    .in17(_18_prime), .in18(_19_prime), .in19(_20_prime), .in20(_21_prime), .in21(_22_prime),
    .in22(_23_prime), .in23(_24_prime), .in24(_25_prime), .in25(_26_prime), .in26(_27_prime),
    .in27(_28_prime), .in28(_29_prime), .in29(_30_prime), .in30(_31_prime), .in31(_32_prime), .out(RD1),
    .sel(A1));  // open: en
  Register #(.width(32)) register_17 (.D(_3), .en(is3), .Q(_3_prime), .clk(clk), .clr(reset));
  Register #(.width(32)) register_18 (.D(_7), .en(is7), .Q(_7_prime), .clk(clk), .clr(reset));
  Register #(.width(32)) register_19 (.D(_11), .en(is11), .Q(_11_prime), .clk(clk), .clr(reset));
  Register #(.width(32)) register_20 (.D(_15), .en(is15), .Q(_15_prime), .clk(clk), .clr(reset));
  Register #(.width(32)) register_21 (.D(_19), .en(is19), .Q(_19_prime), .clk(clk), .clr(reset));
  Register #(.width(32)) register_22 (.D(_23), .en(is23), .Q(_23_prime), .clk(clk), .clr(reset));
  Register #(.width(32)) register_23 (.D(_27), .en(is27), .Q(_27_prime), .clk(clk), .clr(reset));
  Register #(.width(32)) register_24 (.D(_31), .en(is31), .Q(_31_prime), .clk(clk), .clr(reset));
  Register #(.width(32)) register_25 (.D(_4), .en(is4), .Q(_4_prime), .clk(clk), .clr(reset));
  Register #(.width(32)) register_26 (.D(_8), .en(is8), .Q(_8_prime), .clk(clk), .clr(reset));
  Register #(.width(32)) register_27 (.D(_12), .en(is12), .Q(_12_prime), .clk(clk), .clr(reset));
  Register #(.width(32)) register_28 (.D(_16), .en(is16), .Q(_16_prime), .clk(clk), .clr(reset));
  Register #(.width(32)) register_29 (.D(_20), .en(is20), .Q(_20_prime), .clk(clk), .clr(reset));
  Register #(.width(32)) register_30 (.D(_24), .en(is24), .Q(_24_prime), .clk(clk), .clr(reset));
  Register #(.width(32)) register_31 (.D(_28), .en(is28), .Q(_28_prime), .clk(clk), .clr(reset));
  Register #(.width(32)) register_32 (.D(_32), .en(is32), .Q(_32_prime), .clk(clk), .clr(reset));
  Multiplexer #(.select(5), .width(32)) multiplexer_2 (
    .in0(_1_prime), .in1(_2_prime), .in2(_3_prime), .in3(_4_prime), .in4(_5_prime), .in5(_6_prime),
    .in6(_7_prime), .in7(_8_prime), .in8(_9_prime), .in9(_10_prime), .in10(_11_prime), .in11(_12_prime),
    .in12(_13_prime), .in13(_14_prime), .in14(_15_prime), .in15(_16_prime), .in16(_17_prime),
    .in17(_18_prime), .in18(_19_prime), .in19(_20_prime), .in20(_21_prime), .in21(_22_prime),
    .in22(_23_prime), .in23(_24_prime), .in24(_25_prime), .in25(_26_prime), .in26(_27_prime),
    .in27(_28_prime), .in28(_29_prime), .in29(_30_prime), .in30(_31_prime), .in31(_32_prime), .out(RD2),
    .sel(A2));  // open: en

  // Other names for the same wires on the sheet: rst = reset
endmodule

module Controller (
  input  [5:0] Opcode,
  input  [5:0] funct,
  output [1:0] NPCSel,
  output GRFEnable,
  output EXTType,
  output [4:0] Type,
  output ALUIBSel,
  output GRF_A3Sel,
  output DMEnable,
  output DMtoGRFSel,
  output PC_4toGRFSel,
  output raSel,
  output [1:0] StoreType,
  output [1:0] LoadType
);

  wire add, addi, \and , beq, bne, comparator_15_eq, comparator_16_eq, comparator_17_eq, comparator_18_eq,
       comparator_19_eq, comparator_20_eq, comparator_21_eq, isZero, j, jal, jalr, jr, lb, lh, lui, lw, \or ,
       ori, priority_encoder_1_gs, sb, sh, sll, sub, sw;
  wire [4:0] priority_encoder_1_out;

  Comparator #(.width(6), .mode("unsigned")) comparator_1 (.a(Opcode), .b({6{1'b0}}), .eq(isZero));  // open: gt, lt
  Comparator #(.width(6), .mode("unsigned")) comparator_2 (.a(Opcode), .b(6'b001101), .eq(ori));  // open: gt, lt
  Comparator #(.width(6), .mode("unsigned")) comparator_3 (.a(Opcode), .b(6'b100011), .eq(lw));  // open: gt, lt
  Comparator #(.width(6), .mode("unsigned")) comparator_4 (.a(Opcode), .b(6'b101011), .eq(sw));  // open: gt, lt
  Comparator #(.width(6), .mode("unsigned")) comparator_5 (.a(Opcode), .b(6'b000100), .eq(beq));  // open: gt, lt
  Comparator #(.width(6), .mode("unsigned")) comparator_6 (.a(Opcode), .b(6'b001111), .eq(lui));  // open: gt, lt
  Comparator #(.width(6), .mode("unsigned")) comparator_7 (.a(Opcode), .b(6'b001000), .eq(addi));  // open: gt, lt
  Comparator #(.width(6), .mode("unsigned")) comparator_8 (.a(Opcode), .b(6'b000101), .eq(bne));  // open: gt, lt
  Comparator #(.width(6), .mode("unsigned")) comparator_9 (.a(Opcode), .b(6'b000010), .eq(j));  // open: gt, lt
  Comparator #(.width(6), .mode("unsigned")) comparator_10 (.a(Opcode), .b(6'b000011), .eq(jal));  // open: gt, lt
  Comparator #(.width(6), .mode("unsigned")) comparator_11 (.a(Opcode), .b(6'b100000), .eq(lb));  // open: gt, lt
  Comparator #(.width(6), .mode("unsigned")) comparator_12 (.a(Opcode), .b(6'b100001), .eq(lh));  // open: gt, lt
  Comparator #(.width(6), .mode("unsigned")) comparator_13 (.a(Opcode), .b(6'b101000), .eq(sb));  // open: gt, lt
  Comparator #(.width(6), .mode("unsigned")) comparator_14 (.a(Opcode), .b(6'b101001), .eq(sh));  // open: gt, lt
  Comparator #(.width(6), .mode("unsigned")) comparator_15 (
    .a(funct), .b(6'b100000), .eq(comparator_15_eq));  // open: gt, lt
  Comparator #(.width(6), .mode("unsigned")) comparator_16 (
    .a(funct), .b(6'b100010), .eq(comparator_16_eq));  // open: gt, lt
  Comparator #(.width(6), .mode("unsigned")) comparator_17 (
    .a(funct), .b(6'b100100), .eq(comparator_17_eq));  // open: gt, lt
  Comparator #(.width(6), .mode("unsigned")) comparator_18 (
    .a(funct), .b(6'b100101), .eq(comparator_18_eq));  // open: gt, lt
  Comparator #(.width(6), .mode("unsigned")) comparator_19 (
    .a(funct), .b({6{1'b0}}), .eq(comparator_19_eq));  // open: gt, lt
  Comparator #(.width(6), .mode("unsigned")) comparator_20 (
    .a(funct), .b(6'b001001), .eq(comparator_20_eq));  // open: gt, lt
  Comparator #(.width(6), .mode("unsigned")) comparator_21 (
    .a(funct), .b(6'b001000), .eq(comparator_21_eq));  // open: gt, lt
  and and_1 (add, comparator_15_eq, isZero);
  and and_2 (sub, comparator_16_eq, isZero);
  and and_3 (\and , comparator_17_eq, isZero);
  and and_4 (\or , comparator_18_eq, isZero);
  and and_5 (sll, comparator_19_eq, isZero);
  and and_6 (jalr, comparator_20_eq, isZero);
  and and_7 (jr, comparator_21_eq, isZero);
  Priority_Encoder #(.select(5)) priority_encoder_1 (
    .in1(add), .in2(sub), .in3(ori), .in4(sw), .in5(sh), .in6(sb), .in7(lw), .in8(lh), .in9(lb),
    .in10(\and ), .in11(\or ), .in12(j), .in13(jal), .in14(jalr), .in15(jr), .in16(beq), .in17(bne),
    .in18(addi), .in19(lui), .in20(sll), .out(priority_encoder_1_out), .gs(priority_encoder_1_gs));  // open: in0, in21, in22, in23, in24, in25, in26, in27, in28, in29, in30, in31, en_out, en_in
  Multiplexer #(.width(5)) multiplexer_1 (
    .in0({5{1'b0}}), .in1(priority_encoder_1_out), .out(Type), .sel(priority_encoder_1_gs));  // open: en
  Multiplexer #(.select(5), .width(2)) multiplexer_2 (
    .in0(2'b00), .in1(2'b00), .in2(2'b00), .in3(2'b00), .in4(2'b00), .in5(2'b00), .in6(2'b00), .in7(2'b00),
    .in8(2'b00), .in9(2'b00), .in10(2'b00), .in11(2'b00), .in12(2'b01), .in13(2'b01), .in14(2'b10),
    .in15(2'b10), .in16(2'b11), .in17(2'b11), .in18(2'b00), .in19(2'b00), .in20(2'b00), .out(NPCSel),
    .sel(Type));  // open: in21, in22, in23, in24, in25, in26, in27, in28, in29, in30, in31, en
  Multiplexer #(.select(5)) multiplexer_3 (
    .in0(1'b0), .in1(1'b0), .in2(1'b0), .in3(1'b1), .in4(1'b1), .in5(1'b1), .in6(1'b1), .in7(1'b1),
    .in8(1'b1), .in9(1'b1), .in10(1'b0), .in11(1'b0), .in12(1'b0), .in13(1'b0), .in14(1'b0), .in15(1'b0),
    .in16(1'b0), .in17(1'b0), .in18(1'b1), .in19(1'b1), .in20(1'b0), .out(ALUIBSel), .sel(Type));  // open: in21, in22, in23, in24, in25, in26, in27, in28, in29, in30, in31, en
  Multiplexer #(.select(5)) multiplexer_4 (
    .in0(1'b0), .in1(1'b0), .in2(1'b0), .in3(1'b0), .in4(1'b0), .in5(1'b0), .in6(1'b0), .in7(1'b1),
    .in8(1'b1), .in9(1'b1), .in10(1'b0), .in11(1'b0), .in12(1'b0), .in13(1'b0), .in14(1'b0), .in15(1'b0),
    .in16(1'b0), .in17(1'b0), .in18(1'b0), .in19(1'b0), .in20(1'b0), .out(DMtoGRFSel), .sel(Type));  // open: in21, in22, in23, in24, in25, in26, in27, in28, in29, in30, in31, en
  Multiplexer #(.select(5), .width(2)) multiplexer_5 (
    .in0(2'b00), .in1(2'b00), .in2(2'b00), .in3(2'b00), .in4(2'b00), .in5(2'b10), .in6(2'b01), .in7(2'b00),
    .in8(2'b00), .in9(2'b00), .in10(2'b00), .in11(2'b00), .in12(2'b00), .in13(2'b00), .in14(2'b00),
    .in15(2'b00), .in16(2'b00), .in17(2'b00), .in18(2'b00), .in19(2'b00), .in20(2'b00), .out(StoreType),
    .sel(Type));  // open: in21, in22, in23, in24, in25, in26, in27, in28, in29, in30, in31, en
  Multiplexer #(.select(5)) multiplexer_6 (
    .in0(1'b0), .in1(1'b1), .in2(1'b1), .in3(1'b1), .in4(1'b0), .in5(1'b0), .in6(1'b0), .in7(1'b1),
    .in8(1'b1), .in9(1'b1), .in10(1'b1), .in11(1'b1), .in12(1'b0), .in13(1'b1), .in14(1'b1), .in15(1'b0),
    .in16(1'b0), .in17(1'b0), .in18(1'b1), .in19(1'b1), .in20(1'b1), .out(GRFEnable), .sel(Type));  // open: in21, in22, in23, in24, in25, in26, in27, in28, in29, in30, in31, en
  Multiplexer #(.select(5)) multiplexer_7 (
    .in0(1'b0), .in1(1'b1), .in2(1'b1), .in3(1'b0), .in4(1'b0), .in5(1'b0), .in6(1'b0), .in7(1'b0),
    .in8(1'b0), .in9(1'b0), .in10(1'b1), .in11(1'b1), .in12(1'b0), .in13(1'b0), .in14(1'b1), .in15(1'b0),
    .in16(1'b0), .in17(1'b0), .in18(1'b0), .in19(1'b0), .in20(1'b1), .out(GRF_A3Sel), .sel(Type));  // open: in21, in22, in23, in24, in25, in26, in27, in28, in29, in30, in31, en
  Multiplexer #(.select(5)) multiplexer_8 (
    .in0(1'b0), .in1(1'b0), .in2(1'b0), .in3(1'b0), .in4(1'b0), .in5(1'b0), .in6(1'b0), .in7(1'b0),
    .in8(1'b0), .in9(1'b0), .in10(1'b0), .in11(1'b0), .in12(1'b0), .in13(1'b1), .in14(1'b1), .in15(1'b0),
    .in16(1'b0), .in17(1'b0), .in18(1'b0), .in19(1'b0), .in20(1'b0), .out(PC_4toGRFSel), .sel(Type));  // open: in21, in22, in23, in24, in25, in26, in27, in28, in29, in30, in31, en
  Multiplexer #(.select(5), .width(2)) multiplexer_9 (
    .in0(2'b00), .in1(2'b00), .in2(2'b00), .in3(2'b00), .in4(2'b00), .in5(2'b00), .in6(2'b00), .in7(2'b00),
    .in8(2'b10), .in9(2'b01), .in10(2'b00), .in11(2'b00), .in12(2'b00), .in13(2'b00), .in14(2'b00),
    .in15(2'b00), .in16(2'b00), .in17(2'b00), .in18(2'b00), .in19(2'b00), .in20(2'b00), .out(LoadType),
    .sel(Type));  // open: in21, in22, in23, in24, in25, in26, in27, in28, in29, in30, in31, en
  Multiplexer #(.select(5)) multiplexer_10 (
    .in0(1'b0), .in1(1'b0), .in2(1'b0), .in3(1'b0), .in4(1'b1), .in5(1'b1), .in6(1'b1), .in7(1'b1),
    .in8(1'b1), .in9(1'b1), .in10(1'b0), .in11(1'b0), .in12(1'b0), .in13(1'b0), .in14(1'b0), .in15(1'b0),
    .in16(1'b1), .in17(1'b1), .in18(1'b1), .in19(1'b0), .in20(1'b0), .out(EXTType), .sel(Type));  // open: in21, in22, in23, in24, in25, in26, in27, in28, in29, in30, in31, en
  Multiplexer #(.select(5)) multiplexer_11 (
    .in0(1'b0), .in1(1'b0), .in2(1'b0), .in3(1'b0), .in4(1'b1), .in5(1'b1), .in6(1'b1), .in7(1'b0),
    .in8(1'b0), .in9(1'b0), .in10(1'b0), .in11(1'b0), .in12(1'b0), .in13(1'b0), .in14(1'b0), .in15(1'b0),
    .in16(1'b0), .in17(1'b0), .in18(1'b0), .in19(1'b0), .in20(1'b0), .out(DMEnable), .sel(Type));  // open: in21, in22, in23, in24, in25, in26, in27, in28, in29, in30, in31, en
  Multiplexer #(.select(5)) multiplexer_12 (
    .in0(1'b0), .in1(1'b0), .in2(1'b0), .in3(1'b0), .in4(1'b0), .in5(1'b0), .in6(1'b0), .in7(1'b0),
    .in8(1'b0), .in9(1'b0), .in10(1'b0), .in11(1'b0), .in12(1'b0), .in13(1'b1), .in14(1'b0), .in15(1'b0),
    .in16(1'b0), .in17(1'b0), .in18(1'b0), .in19(1'b0), .in20(1'b0), .out(raSel), .sel(Type));  // open: in21, in22, in23, in24, in25, in26, in27, in28, in29, in30, in31, en

  // Notes on the sheet:
  //   忽视即可实现nop
  //   不考虑溢出
  //   lb lh lw 等
  //   0:PC+4  1:imm26  2:Reg  3:imm16
  //   NPCSel
  //   1: imm16   0: rt
  //   ALU inputB Sel
  //   1: Write Data from DM to GRF
  //   DM to GRF Sel
  //   0: origin  1: sb  2: sh
  //   StoreType
  //   1:Allow Write GRF
  //   GRFEnable
  //   1: rd  0: rt
  //   GRF A3 Sel
  //   1: Write PC+4 to GRF
  //   PC + 4 to GRF Sel
  //   jal jalr 等
  //   0: origin  1: lb  2: lh
  //   LoadType
  //   1:signed ext  0:zero  ext
  //   EXTType
  //   sb sh sw 等
  //   1: Select $ra as destination
  //   $raSel
  //   jal
  //   1: Allow Write DM
  //   DMEnable
  //   Type 可做 ALUSel
endmodule

module ALU (
  input  [31:0] A,
  input  [31:0] B,
  input  [4:0] ALUSel,
  input  [4:0] sll,
  output [31:0] \output ,
  output zero
);

  wire AequalsB, Anot_equalsB;
  wire [31:0] A_B, A_B_t, AandB, AorB, B_sll, BLeft16;

  Adder #(.width(32)) adder_1 (.a(A), .b(B), .out(A_B));  // open: cin, cout
  Subtractor #(.width(32)) subtractor_1 (.a(A), .b(B), .out(A_B_t));  // open: bin, bout
  assign AorB = A | B;  // OR_Gate or_1, 32 bits wide
  assign AandB = A & B;  // AND_Gate and_1, 32 bits wide
  Shifter #(.width(32)) shifter_1 (.in(B), .\dist (5'b10000), .out(BLeft16));
  Comparator #(.width(32)) comparator_1 (.a(A), .b(B), .eq(AequalsB));  // open: gt, lt
  Shifter #(.width(32)) shifter_2 (.in(B), .\dist (sll), .out(B_sll));
  not not_1 (Anot_equalsB, AequalsB);
  Multiplexer #(.select(5), .width(32)) multiplexer_1 (
    .in1(A_B), .in2(A_B_t), .in3(AorB), .in4(A_B), .in5(A_B), .in6(A_B), .in7(A_B), .in8(A_B), .in9(A_B),
    .in10(AandB), .in11(AorB), .in18(A_B), .in19(BLeft16), .in20(B_sll), .out(\output ), .sel(ALUSel));  // open: in0, in12, in13, in14, in15, in16, in17, in21, in22, in23, in24, in25, in26, in27, in28, in29, in30, in31, en
  Multiplexer #(.select(5)) multiplexer_2 (
    .in16(AequalsB), .in17(Anot_equalsB), .out(zero), .sel(ALUSel));  // open: in0, in1, in2, in3, in4, in5, in6, in7, in8, in9, in10, in11, in12, in13, in14, in15, in18, in19, in20, in21, in22, in23, in24, in25, in26, in27, in28, in29, in30, in31, en

  // Notes on the sheet:
  //   lui
  //   beq/bne
endmodule

module EXT (
  input  [15:0] imm16,
  input  sel,
  output [31:0] imm32
);

  wire [31:0] bit_extender_1_out, bit_extender_2_out;

  assign bit_extender_1_out = {{16{1'b0}}, imm16};  // Bit_Extender bit_extender_1
  assign bit_extender_2_out = {{16{imm16[15]}}, imm16};  // Bit_Extender bit_extender_2
  Multiplexer #(.width(32)) multiplexer_1 (
    .in0(bit_extender_1_out), .in1(bit_extender_2_out), .out(imm32), .sel(sel));  // open: en
endmodule

module DM (
  input  clk,
  input  reset,
  input  WE,
  input  [31:0] Addr,
  input  [31:0] WD,
  output [31:0] Data
);

  wire [31:0] shifter_1_out;

  Shifter #(.width(32), .shift("lr")) shifter_1 (.in(Addr), .\dist (5'b00010), .out(shifter_1_out));
  RAM #(.addrWidth(12), .dataWidth(32), .bus("separate")) ram_1 (
    .addr(shifter_1_out[11:0]), .din(WD), .data(Data), .str(WE), .clk(clk), .clr(reset));  // open: sel, ld

  // Notes on the sheet:
  //   Data_Mem  3072*32 bit
endmodule

module StoreType (
  input  [31:0] Src,
  input  [31:0] Data,
  input  [31:0] Addr,
  input  [1:0] TypeSel,
  output [31:0] out_5
);

  wire [31:0] SBResult, SHResult;

  Multiplexer #(.select(2), .width(32)) multiplexer_1 (
    .in0({Src[31:8], Data[7:0]}), .in1({Src[31:16], Data[7:0], Src[7:0]}),
    .in2({Src[31:24], Data[7:0], Src[15:0]}), .in3({Data[7:0], Src[23:0]}), .out(SBResult), .sel(Addr[1:0]));  // open: en
  Multiplexer #(.width(32)) multiplexer_2 (
    .in0({Src[31:16], Data[15:0]}), .in1({Data[15:0], Src[15:0]}), .out(SHResult), .sel(Addr[1]));  // open: en
  Multiplexer #(.select(2), .width(32)) multiplexer_3 (
    .in0(Data), .in1(SBResult), .in2(SHResult), .out(out_5), .sel(TypeSel));  // open: in3, en

  // Other names for the same wires on the sheet: forSH[15:0] = Data[15:0]; forSB[7:0] = Data[7:0];
  //   byteSB[1:0] = Addr[1:0]; byteSH = Addr[1]

  // Notes on the sheet:
  //   RAM 中原来的值
  //   要存的数，来自rt
  //   SB
  //   SH
  //   低8位
  //   数据存在高16位
  //   数据存在低16位
  //   高8位
endmodule

module LoadType (
  input  [31:0] Data,
  input  [31:0] Addr,
  input  [1:0] TypeSel,
  output [31:0] out_4
);

  wire [7:0] multiplexer_1_out;
  wire [15:0] multiplexer_2_out;
  wire [31:0] LBResult, LHResult;

  Multiplexer #(.select(2), .width(8)) multiplexer_1 (
    .in0(Data[7:0]), .in1(Data[15:8]), .in2(Data[23:16]), .in3(Data[31:24]), .out(multiplexer_1_out),
    .sel(Addr[1:0]));  // open: en
  Multiplexer #(.width(16)) multiplexer_2 (
    .in0(Data[15:0]), .in1(Data[31:16]), .out(multiplexer_2_out), .sel(Addr[1]));  // open: en
  assign LBResult = {{24{multiplexer_1_out[7]}}, multiplexer_1_out};  // Bit_Extender bit_extender_1
  assign LHResult = {{16{multiplexer_2_out[15]}}, multiplexer_2_out};  // Bit_Extender bit_extender_2
  Multiplexer #(.select(2), .width(32)) multiplexer_3 (
    .in0(Data), .in1(LBResult), .in2(LHResult), .out(out_4), .sel(TypeSel));  // open: in3, en

  // Other names for the same wires on the sheet: byteLB[1:0] = Addr[1:0]; byteLH = Addr[1]; Sel[1:0] = TypeSel

  // Notes on the sheet:
  //   RAM读取的数
endmodule
