// Logisim project prototypeCPU.circ as structural Verilog: 10 circuits, main circuit main
module main (
  input  in_1,
  output [31:0] out_2,
  output [31:0] out_3,
  output out_4,
  output [4:0] out_5,
  output [31:0] out_6,
  output out_7,
  output [31:0] out_8,
  output [31:0] out_9
);

  wire ALUIBSel, clk, EXTSel, MemToRegSel, PCToRegSel, raSel, RegSel, zero;
  wire [1:0] Byte_HalfWordSel, NewPCSel;
  wire [4:0] ALUSel, multiplexer_1_out;
  wire [31:0] dm_1_data, ext_1_imm32, GRF, multiplexer_4_out, multiplexer_5_out, multiplexer_6_out,
       newpc_1_newpc, PC_4, Synthesis;

  Clock clock_1 (.out(clk));
  PC pc_1 (.in_1(clk), .in_2(in_1), .NewPC(newpc_1_newpc), .PC(out_3));
  NewPC newpc_1 (
    .PC(out_3), .NewPC(newpc_1_newpc), .Instr_Index(out_2[25:0]), .GRF(GRF), .sel(NewPCSel),
    .offset(out_2[15:0]), .zero(zero), .out_7(PC_4));
  IM im_1 (.addr(out_3), .instr(out_2));
  Multiplexer #(.width(5), .enable("false")) multiplexer_1 (
    .in0(out_2[20:16]), .in1(out_2[15:11]), .out(multiplexer_1_out), .sel(RegSel));
  Multiplexer #(.width(5)) multiplexer_2 (
    .in0(multiplexer_1_out), .in1({5{1'b1}}), .out(out_5), .sel(raSel));  // open: en
  Controller controller_1 (
    .Opcode(out_2[31:26]), .Funct(out_2[5:0]), .SEL(NewPCSel), .RegWriteEnable(out_4), .ALUType(ALUSel),
    .ExtType(EXTSel), .ALUInputBSel(ALUIBSel), .RegSel(RegSel), .MemWriteEnable(out_7),
    .MemToRegSel(MemToRegSel), .PCToRegSel(PCToRegSel), .raSel(raSel), .Byte_HalfWordSel(Byte_HalfWordSel));
  Multiplexer #(.width(32)) multiplexer_3 (
    .in0(multiplexer_4_out), .in1(PC_4), .out(out_6), .sel(PCToRegSel));  // open: en
  Multiplexer #(.width(32)) multiplexer_4 (
    .in0(out_8), .in1(dm_1_data), .out(multiplexer_4_out), .sel(MemToRegSel));  // open: en
  EXT ext_1 (.imm16(out_2[15:0]), .sel(EXTSel), .imm32(ext_1_imm32));
  GRF grf_1 (
    .clk(clk), .reset(in_1), .WE(out_4), .A1(out_2[25:21]), .A2(out_2[20:16]), .A3(out_5), .WD(out_6),
    .RD1(GRF), .RD2(out_9));
  Multiplexer #(.width(32)) multiplexer_5 (
    .in0(out_9), .in1(ext_1_imm32), .out(multiplexer_5_out), .sel(ALUIBSel));  // open: en
  ALU alu_1 (.A(GRF), .B(multiplexer_5_out), .sel(ALUSel), .\output (out_8), .zero(zero), .sll(out_2[10:6]));
  Multiplexer #(.width(32)) multiplexer_6 (
    .in0(out_9), .in1(Synthesis), .out(multiplexer_6_out), .sel(1'b1));  // open: en
  Byte_HalfWord byte_halfword_1 (
    .Data(out_9), .src(dm_1_data), .Addr(out_8), .DataSel(Byte_HalfWordSel), .out_5(Synthesis));
  DM dm_1 (.clk(clk), .reset(in_1), .WE(out_7), .Addr(out_8), .WD(multiplexer_6_out), .Data(dm_1_data));

  // Other names for the same wires on the sheet: funct[5:0] = out_2[5:0]; imm16[15:0] = out_2[15:0];
  //   imm26[25:0] = out_2[25:0]; Instr[31:0] = out_2; shamt[4:0] = out_2[10:6]; rd[4:0] = out_2[15:11];
  //   rt[4:0] = out_2[20:16]; rs[4:0] = out_2[25:21]; OpCode[5:0] = out_2[31:26]; MemAddr[31:0] = out_8;
  //   MemData[31:0] = out_9; MemWrite = out_7; pc[31:0] = out_3; RegAddr[4:0] = out_5; RegData[31:0] = out_6;
  //   RegWrite = out_4; reset = in_1

  // Notes on the sheet:
  //   IFU
  //   rt
endmodule

module PC (
  input  in_1,
  input  in_2,
  input  [31:0] NewPC,
  output [31:0] PC
);

  wire counter_1_carry;
  wire [31:0] PC_q;

  Register #(.width(32)) u_PC (.D(NewPC), .Q(PC_q), .clk(in_1), .clr(in_2));  // open: en
  Counter #(.width(1), .max('h1), .ongoal("stay")) counter_1 (
    .carry(counter_1_carry), .clk(in_1), .clr(in_2));  // open: load, D, count, Q
  Multiplexer #(.width(32)) multiplexer_1 (.in0(32'h3000), .in1(PC_q), .out(PC), .sel(counter_1_carry));  // open: en

  // Other names for the same wires on the sheet: clk = in_1; reset = in_2
endmodule

module NewPC (
  input  [31:0] PC,
  input  [25:0] Instr_Index,
  input  [31:0] GRF,
  input  [15:0] offset,
  input  [1:0] sel,
  input  zero,
  output [31:0] out_7,
  output [31:0] NewPC
);

  wire [31:0] adder_2_out, bit_extender_1_out, multiplexer_1_out;

  assign bit_extender_1_out = {{14{offset[15]}}, {offset, 2'b00}};  // Bit_Extender bit_extender_1
  Adder #(.width(32)) adder_1 (.a(PC), .b(32'h4), .out(out_7));  // open: cin, cout
  Adder #(.width(32)) adder_2 (.a(out_7), .b(bit_extender_1_out), .out(adder_2_out));  // open: cin, cout
  Multiplexer #(.width(32)) multiplexer_1 (
    .in0(out_7), .in1(adder_2_out), .out(multiplexer_1_out), .sel(zero));  // open: en
  Multiplexer #(.select(2), .width(32)) multiplexer_2 (
    .in0(out_7), .in1({PC[31:28], Instr_Index, 2'b00}), .in2(GRF), .in3(multiplexer_1_out), .out(NewPC),
    .sel(sel));  // open: en

  // Notes on the sheet:
  //   PC+4
endmodule

module IM (
  input  [31:0] addr,
  output [31:0] instr
);

  wire [31:0] shifter_1_out, subtractor_1_out;

  Subtractor #(.width(32)) subtractor_1 (.a(addr), .b(32'h3000), .out(subtractor_1_out));  // open: bin, bout
  Shifter #(.width(32), .shift("lr")) shifter_1 (.in(subtractor_1_out), .\dist (5'b00010), .out(shifter_1_out));
  ROM #(.addrWidth(12), .dataWidth(32)) rom_1 (.addr(shifter_1_out[11:0]), .data(instr));  // open: sel

  // Notes on the sheet:
  //   Instr_Mem     4096*32 bit
  //   contents of rom_1 (hex, n*v repeats v):
  //   3c011234 34285678 a4080064
endmodule

module GRF (
  input  clk,
  input  reset,
  input  WE,
  input  [4:0] A1,
  input  [4:0] A2,
  input  [4:0] A3,
  input  [31:0] WD,
  output [31:0] RD1,
  output [31:0] RD2
);

  wire is2, is3, is4, is5, is6, is7, is8, is9, is10, is11, is12, is13, is14, is15, is16, is17, is18, is19,
       is20, is21, is22, is23, is24, is25, is26, is27, is28, is29, is30, is31, is32;
  wire [31:0] _1, _1_prime, _2, _2_prime, _3, _3_prime, _4, _4_prime, _5, _5_prime, _6, _6_prime, _7,
       _7_prime, _8, _8_prime, _9, _9_prime, _10, _10_prime, _11, _11_prime, _12, _12_prime, _13, _13_prime,
       _14, _14_prime, _15, _15_prime, _16, _16_prime, _17, _17_prime, _18, _18_prime, _19, _19_prime, _20,
       _20_prime, _21, _21_prime, _22, _22_prime, _23, _23_prime, _24, _24_prime, _25, _25_prime, _26,
       _26_prime, _27, _27_prime, _28, _28_prime, _29, _29_prime, _30, _30_prime, _31, _31_prime, _32,
       _32_prime;

  Comparator #(.width(5), .mode("unsigned")) comparator_1 (.a(A3), .b(5'b00001), .eq(is2));  // open: gt, lt
  Comparator #(.width(5), .mode("unsigned")) comparator_2 (.a(A3), .b(5'b00010), .eq(is3));  // open: gt, lt
  Comparator #(.width(5), .mode("unsigned")) comparator_3 (.a(A3), .b(5'b00011), .eq(is4));  // open: gt, lt
  Comparator #(.width(5), .mode("unsigned")) comparator_4 (.a(A3), .b(5'b00100), .eq(is5));  // open: gt, lt
  Comparator #(.width(5), .mode("unsigned")) comparator_5 (.a(A3), .b(5'b00101), .eq(is6));  // open: gt, lt
  Comparator #(.width(5), .mode("unsigned")) comparator_6 (.a(A3), .b(5'b00110), .eq(is7));  // open: gt, lt
  Comparator #(.width(5), .mode("unsigned")) comparator_7 (.a(A3), .b(5'b00111), .eq(is8));  // open: gt, lt
  Comparator #(.width(5), .mode("unsigned")) comparator_8 (.a(A3), .b(5'b01000), .eq(is9));  // open: gt, lt
  Comparator #(.width(5), .mode("unsigned")) comparator_9 (.a(A3), .b(5'b01001), .eq(is10));  // open: gt, lt
  Comparator #(.width(5), .mode("unsigned")) comparator_10 (.a(A3), .b(5'b01010), .eq(is11));  // open: gt, lt
  Comparator #(.width(5), .mode("unsigned")) comparator_11 (.a(A3), .b(5'b01011), .eq(is12));  // open: gt, lt
  Comparator #(.width(5), .mode("unsigned")) comparator_12 (.a(A3), .b(5'b01100), .eq(is13));  // open: gt, lt
  Comparator #(.width(5), .mode("unsigned")) comparator_13 (.a(A3), .b(5'b01101), .eq(is14));  // open: gt, lt
  Comparator #(.width(5), .mode("unsigned")) comparator_14 (.a(A3), .b(5'b01110), .eq(is15));  // open: gt, lt
  Comparator #(.width(5), .mode("unsigned")) comparator_15 (.a(A3), .b(5'b01111), .eq(is16));  // open: gt, lt
  Comparator #(.width(5), .mode("unsigned")) comparator_16 (.a(A3), .b(5'b10000), .eq(is17));  // open: gt, lt
  Comparator #(.width(5), .mode("unsigned")) comparator_17 (.a(A3), .b(5'b10001), .eq(is18));  // open: gt, lt
  Comparator #(.width(5), .mode("unsigned")) comparator_18 (.a(A3), .b(5'b10010), .eq(is19));  // open: gt, lt
  Comparator #(.width(5), .mode("unsigned")) comparator_19 (.a(A3), .b(5'b10011), .eq(is20));  // open: gt, lt
  Comparator #(.width(5), .mode("unsigned")) comparator_20 (.a(A3), .b(5'b10100), .eq(is21));  // open: gt, lt
  Comparator #(.width(5), .mode("unsigned")) comparator_21 (.a(A3), .b(5'b10101), .eq(is22));  // open: gt, lt
  Comparator #(.width(5), .mode("unsigned")) comparator_22 (.a(A3), .b(5'b10110), .eq(is23));  // open: gt, lt
  Comparator #(.width(5), .mode("unsigned")) comparator_23 (.a(A3), .b(5'b10111), .eq(is24));  // open: gt, lt
  Comparator #(.width(5), .mode("unsigned")) comparator_24 (.a(A3), .b(5'b11000), .eq(is25));  // open: gt, lt
  Comparator #(.width(5), .mode("unsigned")) comparator_25 (.a(A3), .b(5'b11001), .eq(is26));  // open: gt, lt
  Comparator #(.width(5), .mode("unsigned")) comparator_26 (.a(A3), .b(5'b11010), .eq(is27));  // open: gt, lt
  Comparator #(.width(5), .mode("unsigned")) comparator_27 (.a(A3), .b(5'b11011), .eq(is28));  // open: gt, lt
  Comparator #(.width(5), .mode("unsigned")) comparator_28 (.a(A3), .b(5'b11100), .eq(is29));  // open: gt, lt
  Comparator #(.width(5), .mode("unsigned")) comparator_29 (.a(A3), .b(5'b11101), .eq(is30));  // open: gt, lt
  Comparator #(.width(5), .mode("unsigned")) comparator_30 (.a(A3), .b(5'b11110), .eq(is31));  // open: gt, lt
  Comparator #(.width(5), .mode("unsigned")) comparator_31 (.a(A3), .b({5{1'b1}}), .eq(is32));  // open: gt, lt
  // Probe on _1
  Demultiplexer #(.select(5), .width(32)) demultiplexer_1 (
    .out0(_1), .out1(_2), .out2(_3), .out3(_4), .out4(_5), .out5(_6), .out6(_7), .out7(_8), .out8(_9),
    .out9(_10), .out10(_11), .out11(_12), .out12(_13), .out13(_14), .out14(_15), .out15(_16), .out16(_17),
    .out17(_18), .out18(_19), .out19(_20), .out20(_21), .out21(_22), .out22(_23), .out23(_24), .out24(_25),
    .out25(_26), .out26(_27), .out27(_28), .out28(_29), .out29(_30), .out30(_31), .out31(_32), .in(WD),
    .sel(A3), .en(WE));
  Register #(.width(32)) register_1 (.D({32{1'b0}}), .Q(_1_prime), .clk(clk), .clr(reset));  // open: en
  Register #(.width(32)) register_2 (.D(_5), .en(is5), .Q(_5_prime), .clk(clk), .clr(reset));
  Register #(.width(32)) register_3 (.D(_9), .en(is9), .Q(_9_prime), .clk(clk), .clr(reset));
  Register #(.width(32)) register_4 (.D(_13), .en(is13), .Q(_13_prime), .clk(clk), .clr(reset));
  Register #(.width(32)) register_5 (.D(_17), .en(is17), .Q(_17_prime), .clk(clk), .clr(reset));
  Register #(.width(32)) register_6 (.D(_21), .en(is21), .Q(_21_prime), .clk(clk), .clr(reset));
  Register #(.width(32)) register_7 (.D(_25), .en(is25), .Q(_25_prime), .clk(clk), .clr(reset));
  Register #(.width(32)) register_8 (.D(_29), .en(is29), .Q(_29_prime), .clk(clk), .clr(reset));
  Register #(.width(32)) register_9 (.D(_2), .en(is2), .Q(_2_prime), .clk(clk), .clr(reset));
  Register #(.width(32)) register_10 (.D(_6), .en(is6), .Q(_6_prime), .clk(clk), .clr(reset));
  Register #(.width(32)) register_11 (.D(_10), .en(is10), .Q(_10_prime), .clk(clk), .clr(reset));
  Register #(.width(32)) register_12 (.D(_14), .en(is14), .Q(_14_prime), .clk(clk), .clr(reset));
  Register #(.width(32)) register_13 (.D(_18), .en(is18), .Q(_18_prime), .clk(clk), .clr(reset));
  Register #(.width(32)) register_14 (.D(_22), .en(is22), .Q(_22_prime), .clk(clk), .clr(reset));
  Register #(.width(32)) register_15 (.D(_26), .en(is26), .Q(_26_prime), .clk(clk), .clr(reset));
  Register #(.width(32)) register_16 (.D(_30), .en(is30), .Q(_30_prime), .clk(clk), .clr(reset));
  Multiplexer #(.select(5), .width(32)) multiplexer_1 (
    .in0(_1_prime), .in1(_2_prime), .in2(_3_prime), .in3(_4_prime), .in4(_5_prime), .in5(_6_prime),
    .in6(_7_prime), .in7(_8_prime), .in8(_9_prime), .in9(_10_prime), .in10(_11_prime), .in11(_12_prime),
    .in12(_13_prime), .in13(_14_prime), .in14(_15_prime), .in15(_16_prime), .in16(_17_prime),
    .in17(_18_prime), .in18(_19_prime), .in19(_20_prime), .in20(_21_prime), .in21(_22_prime),
    .in22(_23_prime), .in23(_24_prime), .in24(_25_prime), .in25(_26_prime), .in26(_27_prime),
    .in27(_28_prime), .in28(_29_prime), .in29(_30_prime), .in30(_31_prime), .in31(_32_prime), .out(RD1),
    .sel(A1));  // open: en
  Register #(.width(32)) register_17 (.D(_3), .en(is3), .Q(_3_prime), .clk(clk), .clr(reset));
  Register #(.width(32)) register_18 (.D(_7), .en(is7), .Q(_7_prime), .clk(clk), .clr(reset));
  Register #(.width(32)) register_19 (.D(_11), .en(is11), .Q(_11_prime), .clk(clk), .clr(reset));
  Register #(.width(32)) register_20 (.D(_15), .en(is15), .Q(_15_prime), .clk(clk), .clr(reset));
  Register #(.width(32)) register_21 (.D(_19), .en(is19), .Q(_19_prime), .clk(clk), .clr(reset));
  Register #(.width(32)) register_22 (.D(_23), .en(is23), .Q(_23_prime), .clk(clk), .clr(reset));
  Register #(.width(32)) register_23 (.D(_27), .en(is27), .Q(_27_prime), .clk(clk), .clr(reset));
  Register #(.width(32)) register_24 (.D(_31), .en(is31), .Q(_31_prime), .clk(clk), .clr(reset));
  Register #(.width(32)) register_25 (.D(_4), .en(is4), .Q(_4_prime), .clk(clk), .clr(reset));
  Register #(.width(32)) register_26 (.D(_8), .en(is8), .Q(_8_prime), .clk(clk), .clr(reset));
  Register #(.width(32)) register_27 (.D(_12), .en(is12), .Q(_12_prime), .clk(clk), .clr(reset));
  Register #(.width(32)) register_28 (.D(_16), .en(is16), .Q(_16_prime), .clk(clk), .clr(reset));
  Register #(.width(32)) register_29 (.D(_20), .en(is20), .Q(_20_prime), .clk(clk), .clr(reset));
  Register #(.width(32)) register_30 (.D(_24), .en(is24), .Q(_24_prime), .clk(clk), .clr(reset));
  Register #(.width(32)) register_31 (.D(_28), .en(is28), .Q(_28_prime), .clk(clk), .clr(reset));
  Register #(.width(32)) register_32 (.D(_32), .en(is32), .Q(_32_prime), .clk(clk), .clr(reset));
  Multiplexer #(.select(5), .width(32)) multiplexer_2 (
    .in0(_1_prime), .in1(_2_prime), .in2(_3_prime), .in3(_4_prime), .in4(_5_prime), .in5(_6_prime),
    .in6(_7_prime), .in7(_8_prime), .in8(_9_prime), .in9(_10_prime), .in10(_11_prime), .in11(_12_prime),
    .in12(_13_prime), .in13(_14_prime), .in14(_15_prime), .in15(_16_prime), .in16(_17_prime),
    .in17(_18_prime), .in18(_19_prime), .in19(_20_prime), .in20(_21_prime), .in21(_22_prime),
    .in22(_23_prime), .in23(_24_prime), .in24(_25_prime), .in25(_26_prime), .in26(_27_prime),
    .in27(_28_prime), .in28(_29_prime), .in29(_30_prime), .in30(_31_prime), .in31(_32_prime), .out(RD2),
    .sel(A2));  // open: en

  // Other names for the same wires on the sheet: rst = reset
endmodule

module Controller (
  input  [5:0] Opcode,
  input  [5:0] Funct,
  output [1:0] SEL,
  output RegWriteEnable,
  output ExtType,
  output [4:0] ALUType,
  output ALUInputBSel,
  output RegSel,
  output MemWriteEnable,
  output MemToRegSel,
  output PCToRegSel,
  output raSel,
  output [1:0] Byte_HalfWordSel
);

  wire add, addi, addiu, addu, \and , andi, beq, bne, comparator_18_eq, comparator_19_eq, comparator_20_eq,
       comparator_21_eq, comparator_22_eq, comparator_23_eq, comparator_24_eq, comparator_25_eq,
       comparator_26_eq, comparator_27_eq, isZero, j, jal, jalr, jr, lb, lh, lui, lw, \or , ori,
       priority_encoder_1_gs, sb, sh, sll, sub, subu, sw, \xor , xori;
  wire [4:0] priority_encoder_1_out;

  Comparator #(.width(6), .mode("unsigned")) comparator_1 (.a(Opcode), .b({6{1'b0}}), .eq(isZero));  // open: gt, lt
  Comparator #(.width(6), .mode("unsigned")) comparator_2 (.a(Opcode), .b(6'b001000), .eq(addi));  // open: gt, lt
  Comparator #(.width(6), .mode("unsigned")) comparator_3 (.a(Opcode), .b(6'b001001), .eq(addiu));  // open: gt, lt
  Comparator #(.width(6), .mode("unsigned")) comparator_4 (.a(Opcode), .b(6'b001100), .eq(andi));  // open: gt, lt
  Comparator #(.width(6), .mode("unsigned")) comparator_5 (.a(Opcode), .b(6'b000100), .eq(beq));  // open: gt, lt
  Comparator #(.width(6), .mode("unsigned")) comparator_6 (.a(Opcode), .b(6'b000101), .eq(bne));  // open: gt, lt
  Comparator #(.width(6), .mode("unsigned")) comparator_7 (.a(Opcode), .b(6'b000010), .eq(j));  // open: gt, lt
  Comparator #(.width(6), .mode("unsigned")) comparator_8 (.a(Opcode), .b(6'b000011), .eq(jal));  // open: gt, lt
  Comparator #(.width(6), .mode("unsigned")) comparator_9 (.a(Opcode), .b(6'b100000), .eq(lb));  // open: gt, lt
  Comparator #(.width(6), .mode("unsigned")) comparator_10 (.a(Opcode), .b(6'b100001), .eq(lh));  // open: gt, lt
  Comparator #(.width(6), .mode("unsigned")) comparator_11 (.a(Opcode), .b(6'b001111), .eq(lui));  // open: gt, lt
  Comparator #(.width(6), .mode("unsigned")) comparator_12 (.a(Opcode), .b(6'b100011), .eq(lw));  // open: gt, lt
  Comparator #(.width(6), .mode("unsigned")) comparator_13 (.a(Opcode), .b(6'b101000), .eq(sb));  // open: gt, lt
  Comparator #(.width(6), .mode("unsigned")) comparator_14 (.a(Opcode), .b(6'b101001), .eq(sh));  // open: gt, lt
  Comparator #(.width(6), .mode("unsigned")) comparator_15 (.a(Opcode), .b(6'b101011), .eq(sw));  // open: gt, lt
  Comparator #(.width(6), .mode("unsigned")) comparator_16 (.a(Opcode), .b(6'b001101), .eq(ori));  // open: gt, lt
  Comparator #(.width(6), .mode("unsigned")) comparator_17 (.a(Opcode), .b(6'b001110), .eq(xori));  // open: gt, lt
  Comparator #(.width(6), .mode("unsigned")) comparator_18 (
    .a(Funct), .b(6'b100000), .eq(comparator_18_eq));  // open: gt, lt
  Comparator #(.width(6), .mode("unsigned")) comparator_19 (
    .a(Funct), .b(6'b100001), .eq(comparator_19_eq));  // open: gt, lt
  Comparator #(.width(6), .mode("unsigned")) comparator_20 (
    .a(Funct), .b(6'b100100), .eq(comparator_20_eq));  // open: gt, lt
  Comparator #(.width(6), .mode("unsigned")) comparator_21 (
    .a(Funct), .b(6'b001001), .eq(comparator_21_eq));  // open: gt, lt
  Comparator #(.width(6), .mode("unsigned")) comparator_22 (
    .a(Funct), .b(6'b001000), .eq(comparator_22_eq));  // open: gt, lt
  Comparator #(.width(6), .mode("unsigned")) comparator_23 (
    .a(Funct), .b(6'b100010), .eq(comparator_23_eq));  // open: gt, lt
  Comparator #(.width(6), .mode("unsigned")) comparator_24 (
    .a(Funct), .b(6'b100011), .eq(comparator_24_eq));  // open: gt, lt
  Comparator #(.width(6), .mode("unsigned")) comparator_25 (
    .a(Funct), .b(6'b100101), .eq(comparator_25_eq));  // open: gt, lt
  Comparator #(.width(6), .mode("unsigned")) comparator_26 (
    .a(Funct), .b(6'b100110), .eq(comparator_26_eq));  // open: gt, lt
  Comparator #(.width(6), .mode("unsigned")) comparator_27 (
    .a(Funct), .b({6{1'b0}}), .eq(comparator_27_eq));  // open: gt, lt
  and and_1 (add, comparator_18_eq, isZero);
  and and_2 (addu, comparator_19_eq, isZero);
  and and_3 (\and , comparator_20_eq, isZero);
  and and_4 (jalr, comparator_21_eq, isZero);
  and and_5 (jr, comparator_22_eq, isZero);
  and and_6 (sub, comparator_23_eq, isZero);
  and and_7 (subu, comparator_24_eq, isZero);
  and and_8 (\or , comparator_25_eq, isZero);
  and and_9 (\xor , comparator_26_eq, isZero);
  and and_10 (sll, comparator_27_eq, isZero);
  // Probe on priority_encoder_1_out
  Priority_Encoder #(.select(5)) priority_encoder_1 (
    .in1(addi), .in2(add), .in3(addiu), .in4(addu), .in5(andi), .in6(\and ), .in7(sub), .in8(subu),
    .in9(\or ), .in10(ori), .in11(\xor ), .in12(xori), .in13(lb), .in14(sb), .in15(lh), .in16(sh), .in17(lw),
    .in18(sw), .in19(lui), .in20(bne), .in21(beq), .in22(j), .in23(jal), .in24(jr), .in25(jalr), .in26(sll),
    .out(priority_encoder_1_out), .gs(priority_encoder_1_gs));  // open: in0, in27, in28, in29, in30, in31, en_out, en_in
  Multiplexer #(.width(5)) multiplexer_1 (
    .in0({5{1'b0}}), .in1(priority_encoder_1_out), .out(ALUType), .sel(priority_encoder_1_gs));  // open: en
  Multiplexer #(.select(5), .width(2)) multiplexer_2 (
    .in0(2'b00), .in1(2'b00), .in2(2'b00), .in3(2'b00), .in4(2'b00), .in5(2'b00), .in6(2'b00), .in7(2'b00),
    .in8(2'b00), .in9(2'b00), .in10(2'b00), .in11(2'b00), .in12(2'b00), .in13(2'b00), .in14(2'b00),
    .in15(2'b00), .in16(2'b00), .in17(2'b00), .in18(2'b00), .in19(2'b00), .in20(2'b11), .in21(2'b11),
    .in22(2'b01), .in23(2'b01), .in24(2'b10), .in25(2'b10), .in26(2'b00), .out(SEL), .sel(ALUType));  // open: in27, in28, in29, in30, in31, en
  Multiplexer #(.select(5)) multiplexer_3 (
    .in0(1'b0), .in1(1'b1), .in2(1'b0), .in3(1'b1), .in4(1'b0), .in5(1'b1), .in6(1'b0), .in7(1'b0),
    .in8(1'b0), .in9(1'b0), .in10(1'b1), .in11(1'b0), .in12(1'b1), .in13(1'b1), .in14(1'b1), .in15(1'b1),
    .in16(1'b1), .in17(1'b1), .in18(1'b1), .in19(1'b1), .in20(1'b0), .in21(1'b0), .in22(1'b0), .in23(1'b0),
    .in24(1'b0), .in25(1'b0), .in26(1'b0), .out(ALUInputBSel), .sel(ALUType));  // open: in27, in28, in29, in30, in31, en
  Multiplexer #(.select(5)) multiplexer_4 (
    .in0(1'b0), .in1(1'b0), .in2(1'b0), .in3(1'b0), .in4(1'b0), .in5(1'b0), .in6(1'b0), .in7(1'b0),
    .in8(1'b0), .in9(1'b0), .in10(1'b0), .in11(1'b0), .in12(1'b0), .in13(1'b1), .in14(1'b0), .in15(1'b1),
    .in16(1'b0), .in17(1'b1), .in18(1'b0), .in19(1'b0), .in20(1'b0), .in21(1'b0), .in22(1'b0), .in23(1'b0),
    .in24(1'b0), .in25(1'b0), .in26(1'b0), .out(MemToRegSel), .sel(ALUType));  // open: in27, in28, in29, in30, in31, en
  Multiplexer #(.select(5), .width(2)) multiplexer_5 (
    .in0(2'b00), .in1(2'b00), .in2(2'b00), .in3(2'b00), .in4(2'b00), .in5(2'b00), .in6(2'b00), .in7(2'b00),
    .in8(2'b00), .in9(2'b00), .in10(2'b00), .in11(2'b00), .in12(2'b00), .in13(2'b01), .in14(2'b01),
    .in15(2'b10), .in16(2'b10), .in17(2'b00), .in18(2'b00), .in19(2'b00), .in20(2'b00), .in21(2'b00),
    .in22(2'b00), .in23(2'b00), .in24(2'b00), .in25(2'b00), .in26(2'b00), .out(Byte_HalfWordSel),
    .sel(ALUType));  // open: in27, in28, in29, in30, in31, en
  Multiplexer #(.select(5)) multiplexer_6 (
    .in0(1'b0), .in1(1'b1), .in2(1'b1), .in3(1'b1), .in4(1'b1), .in5(1'b1), .in6(1'b1), .in7(1'b1),
    .in8(1'b1), .in9(1'b1), .in10(1'b1), .in11(1'b1), .in12(1'b1), .in13(1'b1), .in14(1'b0), .in15(1'b1),
    .in16(1'b0), .in17(1'b1), .in18(1'b0), .in19(1'b1), .in20(1'b0), .in21(1'b0), .in22(1'b0), .in23(1'b1),
    .in24(1'b0), .in25(1'b1), .in26(1'b1), .out(RegWriteEnable), .sel(ALUType));  // open: in27, in28, in29, in30, in31, en
  Multiplexer #(.select(5)) multiplexer_7 (
    .in0(1'b0), .in1(1'b0), .in2(1'b1), .in3(1'b0), .in4(1'b1), .in5(1'b0), .in6(1'b1), .in7(1'b1),
    .in8(1'b1), .in9(1'b1), .in10(1'b0), .in11(1'b1), .in12(1'b0), .in13(1'b0), .in14(1'b0), .in15(1'b0),
    .in16(1'b0), .in17(1'b0), .in18(1'b0), .in19(1'b0), .in20(1'b0), .in21(1'b0), .in22(1'b0), .in23(1'b0),
    .in24(1'b0), .in25(1'b1), .in26(1'b1), .out(RegSel), .sel(ALUType));  // open: in27, in28, in29, in30, in31, en
  Multiplexer #(.select(5)) multiplexer_8 (
    .in0(1'b0), .in1(1'b0), .in2(1'b0), .in3(1'b0), .in4(1'b0), .in5(1'b0), .in6(1'b0), .in7(1'b0),
    .in8(1'b0), .in9(1'b0), .in10(1'b0), .in11(1'b0), .in12(1'b0), .in13(1'b0), .in14(1'b0), .in15(1'b0),
    .in16(1'b0), .in17(1'b0), .in18(1'b0), .in19(1'b0), .in20(1'b0), .in21(1'b0), .in22(1'b0), .in23(1'b1),
    .in24(1'b0), .in25(1'b1), .in26(1'b0), .out(PCToRegSel), .sel(ALUType));  // open: in27, in28, in29, in30, in31, en
  Multiplexer #(.select(5)) multiplexer_9 (
    .in0(1'b0), .in1(1'b1), .in2(1'b0), .in3(1'b0), .in4(1'b0), .in5(1'b0), .in6(1'b0), .in7(1'b0),
    .in8(1'b0), .in9(1'b0), .in10(1'b0), .in11(1'b0), .in12(1'b0), .in13(1'b1), .in14(1'b1), .in15(1'b1),
    .in16(1'b1), .in17(1'b1), .in18(1'b1), .in19(1'b0), .in20(1'b0), .in21(1'b0), .in22(1'b0), .in23(1'b1),
    .in24(1'b0), .in25(1'b1), .in26(1'b0), .out(ExtType), .sel(ALUType));  // open: in27, in28, in29, in30, in31, en
  Multiplexer #(.select(5)) multiplexer_10 (
    .in0(1'b0), .in1(1'b0), .in2(1'b0), .in3(1'b0), .in4(1'b0), .in5(1'b0), .in6(1'b0), .in7(1'b0),
    .in8(1'b0), .in9(1'b0), .in10(1'b0), .in11(1'b0), .in12(1'b0), .in13(1'b0), .in14(1'b1), .in15(1'b0),
    .in16(1'b1), .in17(1'b0), .in18(1'b1), .in19(1'b0), .in20(1'b0), .in21(1'b0), .in22(1'b0), .in23(1'b0),
    .in24(1'b0), .in25(1'b0), .in26(1'b0), .out(MemWriteEnable), .sel(ALUType));  // open: in27, in28, in29, in30, in31, en
  Multiplexer #(.select(5)) multiplexer_11 (
    .in0(1'b0), .in1(1'b0), .in2(1'b0), .in3(1'b0), .in4(1'b0), .in5(1'b0), .in6(1'b0), .in7(1'b0),
    .in8(1'b0), .in9(1'b0), .in10(1'b0), .in11(1'b0), .in12(1'b0), .in13(1'b0), .in14(1'b0), .in15(1'b0),
    .in16(1'b0), .in17(1'b0), .in18(1'b0), .in19(1'b0), .in20(1'b0), .in21(1'b0), .in22(1'b0), .in23(1'b1),
    .in24(1'b0), .in25(1'b0), .in26(1'b0), .out(raSel), .sel(ALUType));  // open: in27, in28, in29, in30, in31, en

  // Notes on the sheet:
  //   0:PC+4  1:PC=imm26  2:PC=Reg  3:PC=imm16
  //   NewPCSel
  //   unknown opcode
  //   imm(1) or rt(0)
  //   MemToRegSel
  //   0: SrcData  1: Byte  2: HalfWord
  //   unknown opcode
  //   RegWriteEnable
  //   rd(1) or rt(0)
  //   PCToRegSel
  //   sigend_ext(1) or zero_ext(0)
  //   MemWriteEnable
  //   $raSel
endmodule

module ALU (
  input  [31:0] A,
  input  [31:0] B,
  input  [4:0] sel,
  input  [4:0] sll,
  output [31:0] \output ,
  output zero
);

  wire AequalsB, Anot_equalsB;
  wire [31:0] A_B, A_B_t, AandB, AorB, AxorB, B_sll, BLeft16;

  Adder #(.width(32)) adder_1 (.a(A), .b(B), .out(A_B));  // open: cin, cout
  Subtractor #(.width(32)) subtractor_1 (.a(A), .b(B), .out(A_B_t));  // open: bin, bout
  assign AorB = A | B;  // OR_Gate or_1, 32 bits wide
  assign AxorB = A ^ B;  // XOR_Gate xor_1, 32 bits wide
  Shifter #(.width(32)) shifter_1 (.in(B), .\dist (5'b10000), .out(BLeft16));
  Comparator #(.width(32)) comparator_1 (.a(A), .b(B), .eq(AequalsB));  // open: gt, lt
  Shifter #(.width(32)) shifter_2 (.in(B), .\dist (sll), .out(B_sll));
  not not_1 (Anot_equalsB, AequalsB);
  assign AandB = A & B;  // AND_Gate and_1, 32 bits wide
  Multiplexer #(.select(5), .width(32)) multiplexer_1 (
    .in1(A_B), .in2(A_B), .in3(A_B), .in4(A_B), .in5(AandB), .in6(AandB), .in7(A_B_t), .in8(A_B_t),
    .in9(AorB), .in10(AorB), .in11(AxorB), .in12(AxorB), .in14(A_B), .in16(A_B), .in17(A_B), .in18(A_B),
    .in19(BLeft16), .in26(B_sll), .out(\output ), .sel(sel));  // open: in0, in13, in15, in20, in21, in22, in23, in24, in25, in27, in28, in29, in30, in31, en
  Multiplexer #(.select(5)) multiplexer_2 (
    .in20(Anot_equalsB), .in21(AequalsB), .out(zero), .sel(sel));  // open: in0, in1, in2, in3, in4, in5, in6, in7, in8, in9, in10, in11, in12, in13, in14, in15, in16, in17, in18, in19, in22, in23, in24, in25, in26, in27, in28, in29, in30, in31, en
endmodule

module EXT (
  input  [15:0] imm16,
  input  sel,
  output [31:0] imm32
);

  wire [31:0] bit_extender_1_out, bit_extender_2_out;

  assign bit_extender_1_out = {{16{1'b0}}, imm16};  // Bit_Extender bit_extender_1
  assign bit_extender_2_out = {{16{imm16[15]}}, imm16};  // Bit_Extender bit_extender_2
  Multiplexer #(.width(32)) multiplexer_1 (
    .in0(bit_extender_1_out), .in1(bit_extender_2_out), .out(imm32), .sel(sel));  // open: en
endmodule

module DM (
  input  clk,
  input  reset,
  input  WE,
  input  [31:0] Addr,
  input  [31:0] WD,
  output [31:0] Data
);

  wire [31:0] shifter_1_out;

  Shifter #(.width(32), .shift("lr")) shifter_1 (.in(Addr), .\dist (5'b00010), .out(shifter_1_out));
  RAM #(.addrWidth(12), .dataWidth(32), .bus("separate")) ram_1 (
    .addr(shifter_1_out[11:0]), .din(WD), .data(Data), .str(WE), .clk(clk), .clr(reset));  // open: sel, ld

  // Notes on the sheet:
  //   Data_Mem  3072*32 bit
endmodule

module Byte_HalfWord (
  input  [31:0] Data,
  input  [31:0] Addr,
  input  [31:0] src,
  input  [1:0] DataSel,
  output [31:0] out_5
);

  wire [4:0] \byte , halfword, multiplier_1_out, multiplier_2_out, multiplier_3_out, multiplier_4_out;
  wire [31:0] and_1_out, and_2_out, bit_extender_3_out, bit_extender_4_out, data_t, multiplexer_1_out,
       or_1_out, or_2_out, shifter_1_out, shifter_2_out, shifter_3_out, shifter_4_out;

  assign \byte  = {{3{1'b0}}, Addr[1:0]};  // Bit_Extender bit_extender_1
  assign halfword = {{4{1'b0}}, Addr[1]};  // Bit_Extender bit_extender_2
  assign bit_extender_3_out = {{24{1'b0}}, Data[7:0]};  // Bit_Extender bit_extender_3
  assign bit_extender_4_out = {{16{1'b0}}, Data[15:0]};  // Bit_Extender bit_extender_4
  Multiplexer #(.select(2), .width(32)) multiplexer_1 (
    .in0(Data), .in1(bit_extender_3_out), .in2(bit_extender_4_out), .out(multiplexer_1_out), .sel(DataSel));  // open: in3, en
  // Probe on shifter_3_out
  Multiplier #(.width(5)) multiplier_1 (.a(\byte ), .b(5'b01000), .out(multiplier_1_out));  // open: cin, cout
  Multiplier #(.width(5)) multiplier_2 (.a(halfword), .b(5'b10000), .out(multiplier_2_out));  // open: cin, cout
  Shifter #(.width(32), .shift("rl")) shifter_1 (.in(32'hffffff00), .\dist (multiplier_3_out), .out(shifter_1_out));
  Multiplier #(.width(5)) multiplier_3 (.a(\byte ), .b(5'b01000), .out(multiplier_3_out));  // open: cin, cout
  Shifter #(.width(32), .shift("rl")) shifter_2 (.in(32'hffff0000), .\dist (multiplier_4_out), .out(shifter_2_out));
  Multiplier #(.width(5)) multiplier_4 (.a(halfword), .b(5'b10000), .out(multiplier_4_out));  // open: cin, cout
  Shifter #(.width(32), .shift("rl")) shifter_3 (
    .in(multiplexer_1_out), .\dist (multiplier_1_out), .out(shifter_3_out));
  Shifter #(.width(32), .shift("rl")) shifter_4 (
    .in(multiplexer_1_out), .\dist (multiplier_2_out), .out(shifter_4_out));
  Multiplexer #(.select(2), .width(32)) multiplexer_2 (
    .in0(multiplexer_1_out), .in1(shifter_3_out), .in2(shifter_4_out), .out(data_t), .sel(DataSel));  // open: in3, en
  assign and_1_out = src & shifter_1_out;  // AND_Gate and_1, 32 bits wide
  assign and_2_out = src & shifter_2_out;  // AND_Gate and_2, 32 bits wide
  assign or_1_out = data_t | and_1_out;  // OR_Gate or_1, 32 bits wide
  assign or_2_out = data_t | and_2_out;  // OR_Gate or_2, 32 bits wide
  Multiplexer #(.select(2), .width(32)) multiplexer_3 (
    .in0(data_t), .in1(or_1_out), .in2(or_2_out), .out(out_5), .sel(DataSel));  // open: in3, en
endmodule
