// Logisim project Sokoban.circ as structural Verilog: 3 circuits, main circuit Sokoban
module Sokoban (
  input  dx,
  input  dy,
  input  clk,
  input  reset,
  output out,
  output flag
);

  wire comparator_1_eq, comparator_2_eq, invalid;
  wire [2:0] bit_extender_1_out, bit_extender_2_out, multiplexer_1_out, multiplexer_2_out, new_x, new_y, x, y;

  check check_1 (.x(new_x), .y(new_y), .out_3(invalid));
  assign bit_extender_1_out = {{2{1'b0}}, dx};  // Bit_Extender bit_extender_1
  assign bit_extender_2_out = {{2{1'b0}}, dy};  // Bit_Extender bit_extender_2
  \new  new_1 (.x(bit_extender_1_out), .dx(x), .new_x(new_x));
  \new  new_2 (.x(bit_extender_2_out), .dx(y), .new_x(new_y));
  Multiplexer #(.width(3)) multiplexer_1 (.in0(new_x), .in1(x), .out(multiplexer_1_out), .sel(invalid));  // open: en
  Multiplexer #(.width(3)) multiplexer_2 (.in0(new_y), .in1(y), .out(multiplexer_2_out), .sel(invalid));  // open: en
  Register #(.width(3)) u_x (.D(multiplexer_1_out), .Q(x), .clk(clk), .clr(reset));  // open: en
  Register #(.width(3)) u_y (.D(multiplexer_2_out), .Q(y), .clk(clk), .clr(reset));  // open: en
  Comparator #(.width(3), .mode("unsigned")) comparator_1 (.a(x), .b(3'b101), .eq(comparator_1_eq));  // open: gt, lt
  Comparator #(.width(3), .mode("unsigned")) comparator_2 (.a(y), .b(3'b101), .eq(comparator_2_eq));  // open: gt, lt
  Register #(.width(1)) register_1 (.D(invalid), .Q(flag), .clk(clk), .clr(reset));  // open: en
  and and_1 (out, comparator_1_eq, comparator_2_eq);

  // Other names for the same wires on the sheet: rst = reset
endmodule

module \new  (
  input  [2:0] x,
  input  [2:0] dx,
  output [2:0] new_x
);

  Adder #(.width(3)) adder_1 (.a(x), .b(dx), .out(new_x));  // open: cin, cout
endmodule

module check (
  input  [2:0] x,
  input  [2:0] y,
  output out_3
);

  wire and_1_out, and_2_out, and_3_out, and_4_out, and_5_out, and_6_out, comparator_1_eq, comparator_2_eq,
       comparator_3_eq, comparator_4_eq, comparator_5_eq, comparator_6_eq, comparator_7_eq, comparator_8_eq,
       comparator_9_eq, comparator_10_eq, comparator_11_eq, comparator_12_eq, comparator_13_gt,
       comparator_14_gt, or_1_out, or_2_out;

  Comparator #(.width(3), .mode("unsigned")) comparator_1 (.a(x), .b(3'b001), .eq(comparator_1_eq));  // open: gt, lt
  Comparator #(.width(3), .mode("unsigned")) comparator_2 (.a(y), .b(3'b001), .eq(comparator_2_eq));  // open: gt, lt
  Comparator #(.width(3), .mode("unsigned")) comparator_3 (.a(x), .b(3'b001), .eq(comparator_3_eq));  // open: gt, lt
  Comparator #(.width(3), .mode("unsigned")) comparator_4 (.a(y), .b(3'b010), .eq(comparator_4_eq));  // open: gt, lt
  Comparator #(.width(3), .mode("unsigned")) comparator_5 (.a(x), .b(3'b010), .eq(comparator_5_eq));  // open: gt, lt
  Comparator #(.width(3), .mode("unsigned")) comparator_6 (.a(y), .b(3'b001), .eq(comparator_6_eq));  // open: gt, lt
  Comparator #(.width(3), .mode("unsigned")) comparator_7 (.a(x), .b(3'b100), .eq(comparator_7_eq));  // open: gt, lt
  Comparator #(.width(3), .mode("unsigned")) comparator_8 (.a(y), .b(3'b100), .eq(comparator_8_eq));  // open: gt, lt
  Comparator #(.width(3), .mode("unsigned")) comparator_9 (.a(x), .b(3'b100), .eq(comparator_9_eq));  // open: gt, lt
  Comparator #(.width(3), .mode("unsigned")) comparator_10 (.a(y), .b(3'b011), .eq(comparator_10_eq));  // open: gt, lt
  Comparator #(.width(3), .mode("unsigned")) comparator_11 (.a(x), .b(3'b011), .eq(comparator_11_eq));  // open: gt, lt
  Comparator #(.width(3), .mode("unsigned")) comparator_12 (.a(y), .b(3'b100), .eq(comparator_12_eq));  // open: gt, lt
  Comparator #(.width(3), .mode("unsigned")) comparator_13 (.a(x), .b(3'b101), .gt(comparator_13_gt));  // open: eq, lt
  Comparator #(.width(3), .mode("unsigned")) comparator_14 (.a(y), .b(3'b101), .gt(comparator_14_gt));  // open: eq, lt
  and and_1 (and_1_out, comparator_1_eq, comparator_2_eq);
  and and_2 (and_2_out, comparator_3_eq, comparator_4_eq);
  and and_3 (and_3_out, comparator_5_eq, comparator_6_eq);
  and and_4 (and_4_out, comparator_7_eq, comparator_8_eq);
  and and_5 (and_5_out, comparator_9_eq, comparator_10_eq);
  and and_6 (and_6_out, comparator_11_eq, comparator_12_eq);
  or or_1 (or_1_out, and_1_out, and_2_out, and_3_out, and_4_out, and_5_out, and_6_out);
  or or_2 (or_2_out, comparator_13_gt, comparator_14_gt);
  or or_3 (out_3, or_1_out, or_2_out);

  // Notes on the sheet:
  //   (1,1)
  //   (1,2)
  //   (2,1)
  //   (4,4)
  //   (4,3)
  //   (3,4)
endmodule
