// Logisim project fibonacci.circ as structural Verilog: 3 circuits, main circuit main
module main (
  input  [2:0] N,
  output [3:0] Nth
);

  wire clock_1_out, time_ctrl_output_signal;

  Clock clock_1 (.out(clock_1_out));
  \time  time_ctrl (.\input (N), .clk(clock_1_out), .output_signal(time_ctrl_output_signal));
  cal cal (.output_signal(time_ctrl_output_signal), .clk(clock_1_out), .Nth(Nth));  // open: reset
endmodule

module \time  (
  input  [2:0] \input ,
  input  clk,
  output output_signal
);

  wire [3:0] bit_extender_1_out, counter_1_q;

  assign bit_extender_1_out = {{1{1'b0}}, \input };  // Bit_Extender bit_extender_1
  Counter #(.width(4), .max('hf), .ongoal("stay")) counter_1 (
    .Q(counter_1_q), .clk(clk));  // open: load, D, count, carry, clr
  Comparator #(.width(4), .mode("unsigned")) comparator_1 (
    .a(bit_extender_1_out), .b(counter_1_q), .lt(output_signal));  // open: gt, eq
endmodule

module cal (
  input  output_signal,
  input  reset,
  input  clk,
  output [3:0] Nth
);

  wire enable, init;
  wire [3:0] adder_1_out, cur, multiplexer_1_out, prev;

  Counter #(.width(1), .max('h1), .ongoal("stay")) counter_1 (.carry(init), .clk(clk));  // open: load, D, count, Q, clr
  // Probe on prev
  // Probe on cur
  not not_1 (enable, output_signal);
  // Probe on multiplexer_1_out
  Multiplexer #(.width(4)) multiplexer_1 (.in0(4'b0001), .in1(cur), .out(multiplexer_1_out), .sel(init));  // open: en
  Adder #(.width(4)) adder_1 (.a(prev), .b(cur), .out(adder_1_out));  // open: cin, cout
  // Probe on prev
  Register #(.width(4)) u_prev (.D(multiplexer_1_out), .en(enable), .Q(prev), .clk(clk), .clr(reset));
  Register #(.width(4)) u_cur (.D(adder_1_out), .en(enable), .Q(cur), .clk(clk), .clr(reset));
  // Probe on cur
  Multiplexer #(.width(4)) multiplexer_2 (.in0(4'b0000), .in1(cur), .out(Nth), .sel(output_signal));  // open: en
endmodule
