// Logisim project fsm.circ as structural Verilog: 2 circuits, main circuit fsm
module fsm (
  input  CLR,
  input  [1:0] In,
  output Z
);

  wire clk, comparator_1_eq, comparator_2_eq, comparator_3_eq, or_1_out, state_hi, state_lo;
  wire [1:0] multiplexer_1_out, n_state;

  Clock u_clk (.out(clk));
  state trans (
    .in_hi(In[1]), .in_lo(In[0]), .state_hi(state_hi), .state_lo(state_lo), .n_state_hi(n_state[1]),
    .n_state_lo(n_state[0]));
  Multiplexer #(.width(2)) multiplexer_1 (.in0(n_state), .in1(2'b00), .out(multiplexer_1_out), .sel(CLR));  // open: en
  Register #(.width(2)) state (.D(multiplexer_1_out), .Q({state_hi, state_lo}), .clk(clk));  // open: en, clr
  Comparator #(.width(2), .mode("unsigned")) comparator_1 (.a(In), .b(2'b10), .eq(comparator_1_eq));  // open: gt, lt
  Comparator #(.width(2), .mode("unsigned")) comparator_2 (.a(In), .b(2'b00), .eq(comparator_2_eq));  // open: gt, lt
  Comparator #(.width(2), .mode("unsigned")) comparator_3 (
    .a({state_hi, state_lo}), .b(2'b10), .eq(comparator_3_eq));  // open: gt, lt
  or or_1 (or_1_out, comparator_1_eq, comparator_2_eq);
  and and_1 (Z, or_1_out, comparator_3_eq);

  // Other names for the same wires on the sheet: in_lo = In[0]; in_hi = In[1]

  // Notes on the sheet:
  //   a:00 b:01 c:10 invalid:11
endmodule

module state (
  input  in_hi,
  input  in_lo,
  input  state_hi,
  input  state_lo,
  output n_state_hi,
  output n_state_lo
);

  wire and_1_out, and_2_out, and_3_out, and_4_out, not_1_out, not_2_out, not_3_out, not_4_out, not_5_out,
       not_6_out, not_7_out;

  not not_1 (not_1_out, in_lo);
  not not_2 (not_2_out, state_hi);
  and and_1 (and_1_out, not_1_out, not_2_out, state_lo);
  not not_3 (not_3_out, in_lo);
  and and_2 (and_2_out, not_3_out, state_hi, not_4_out);
  not not_4 (not_4_out, state_lo);
  not not_5 (not_5_out, in_lo);
  and and_3 (and_3_out, not_5_out, state_hi, not_6_out);
  not not_6 (not_6_out, state_lo);
  not not_7 (not_7_out, in_hi);
  and and_4 (and_4_out, not_7_out, in_lo);
  or or_1 (n_state_hi, and_1_out, and_2_out);
  or or_2 (n_state_lo, and_3_out, and_4_out);
endmodule
