// Logisim project ftoi.circ as structural Verilog: 2 circuits, main circuit ftoi
module ftoi (
  input  [15:0] float,
  output [31:0] \int 
);

  wire checkstyle_1_infinity, checkstyle_1_nan, is_INF_or_NaN, isDN, isN, less_than_0, or_2_out;
  wire [1:1] multiplexer_1_out;
  wire [4:0] select, subtractor_1_out;
  wire [31:0] bit_extender_1_out, bit_extender_2_out, bit_extender_3_out, bit_extender_4_out,
       bit_extender_5_out, bit_extender_6_out, bit_extender_7_out, bit_extender_8_out, bit_extender_9_out,
       bit_extender_10_out, bit_extender_11_out, multiplexer_3_out, multiplexer_4_out, negator_1_out,
       shifter_1_out, shifter_2_out, shifter_3_out, shifter_4_out, shifter_5_out, shifter_6_out,
       shifter_7_out;

  checkstyle checkstyle_1 (
    .E(float[14:10]), .M(float[9:0]), .NaN(checkstyle_1_nan), .Denormalized(isDN),
    .Infinity(checkstyle_1_infinity), .Normalized(isN));
  Subtractor #(.width(5)) subtractor_1 (.a(float[14:10]), .b(5'b01111), .out(subtractor_1_out));  // open: bin, bout
  // Probe on subtractor_1_out
  // Probe on float[9:0]
  Multiplexer multiplexer_1 (.in0(1'b1), .in1(1'b0), .out(multiplexer_1_out[1]), .sel(isDN));  // open: en
  Comparator #(.width(5)) comparator_1 (.a(subtractor_1_out), .b({5{1'b0}}), .lt(less_than_0));  // open: gt, eq
  or or_1 (is_INF_or_NaN, checkstyle_1_nan, checkstyle_1_infinity);
  Multiplexer #(.width(5)) multiplexer_2 (
    .in0(subtractor_1_out), .in1({5{1'b0}}), .out(select), .sel(less_than_0));  // open: en
  // Probe on {multiplexer_1_out[1], float[9]}
  // Probe on {multiplexer_1_out[1], float[9:8]}
  // Probe on {multiplexer_1_out[1], float[9:7]}
  assign bit_extender_1_out = {{21{1'b0}}, {multiplexer_1_out[1], float[9:0]}};  // Bit_Extender bit_extender_1
  assign bit_extender_2_out = {{22{1'b0}}, {multiplexer_1_out[1], float[9:1]}};  // Bit_Extender bit_extender_2
  assign bit_extender_3_out = {{23{1'b0}}, {multiplexer_1_out[1], float[9:2]}};  // Bit_Extender bit_extender_3
  // Probe on bit_extender_1_out
  assign bit_extender_4_out = {{24{1'b0}}, {multiplexer_1_out[1], float[9:3]}};  // Bit_Extender bit_extender_4
  assign bit_extender_5_out = {{25{1'b0}}, {multiplexer_1_out[1], float[9:4]}};  // Bit_Extender bit_extender_5
  assign bit_extender_6_out = {{26{1'b0}}, {multiplexer_1_out[1], float[9:5]}};  // Bit_Extender bit_extender_6
  assign bit_extender_7_out = {{31{1'b0}}, multiplexer_1_out[1]};  // Bit_Extender bit_extender_7
  assign bit_extender_8_out = {{27{1'b0}}, {multiplexer_1_out[1], float[9:6]}};  // Bit_Extender bit_extender_8
  assign bit_extender_9_out = {{28{1'b0}}, {multiplexer_1_out[1], float[9:7]}};  // Bit_Extender bit_extender_9
  // Probe on bit_extender_7_out
  assign bit_extender_10_out = {{29{1'b0}}, {multiplexer_1_out[1], float[9:8]}};  // Bit_Extender bit_extender_10
  assign bit_extender_11_out = {{30{1'b0}}, {multiplexer_1_out[1], float[9]}};  // Bit_Extender bit_extender_11
  Shifter #(.width(32)) shifter_1 (.in(shifter_2_out), .\dist (5'b00001), .out(shifter_1_out));
  Shifter #(.width(32)) shifter_2 (.in(bit_extender_1_out), .\dist (5'b00001), .out(shifter_2_out));
  Shifter #(.width(32)) shifter_3 (.in(shifter_1_out), .\dist (5'b00001), .out(shifter_3_out));
  Shifter #(.width(32)) shifter_4 (.in(shifter_3_out), .\dist (5'b00001), .out(shifter_4_out));
  Shifter #(.width(32)) shifter_5 (.in(shifter_4_out), .\dist (5'b00001), .out(shifter_5_out));
  Shifter #(.width(32)) shifter_6 (.in(shifter_5_out), .\dist (5'b00001), .out(shifter_6_out));
  Shifter #(.width(32)) shifter_7 (.in(shifter_6_out), .\dist (5'b00001), .out(shifter_7_out));
  // Probe on select
  Multiplexer #(.select(5), .width(32)) multiplexer_3 (
    .in0(bit_extender_7_out), .in1(bit_extender_11_out), .in2(bit_extender_10_out), .in3(bit_extender_9_out),
    .in4(bit_extender_8_out), .in5(bit_extender_6_out), .in6(bit_extender_5_out), .in7(bit_extender_4_out),
    .in8(bit_extender_3_out), .in9(bit_extender_2_out), .in10(bit_extender_1_out), .in11(shifter_2_out),
    .in12(shifter_1_out), .in13(shifter_3_out), .in14(shifter_4_out), .in15(shifter_5_out),
    .in16(shifter_6_out), .in17(shifter_7_out), .out(multiplexer_3_out), .sel(select));  // open: in18, in19, in20, in21, in22, in23, in24, in25, in26, in27, in28, in29, in30, in31, en
  Multiplexer #(.width(32)) multiplexer_4 (
    .in0(multiplexer_3_out), .in1({32{1'b0}}), .out(multiplexer_4_out), .sel(or_2_out));  // open: en
  or or_2 (or_2_out, is_INF_or_NaN, less_than_0);
  Negator #(.width(32)) negator_1 (.in(multiplexer_4_out), .out(negator_1_out));
  Multiplexer #(.width(32)) multiplexer_5 (
    .in0(multiplexer_4_out), .in1(negator_1_out), .out(\int ), .sel(float[15]));  // open: en

  // Other names for the same wires on the sheet: M[9:0] = float[9:0]; Ans[31:0] = \int ; E[4:0] = float[14:10];
  //   S = float[15]

  // Notes on the sheet:
  //   S
  //   E
  //   M
endmodule

module checkstyle (
  input  [4:0] E,
  input  [9:0] M,
  output NaN,
  output Denormalized,
  output Infinity,
  output Normalized
);

  wire comparator_2_eq, comparator_3_eq, not_1_out, not_2_out, not_3_out;

  Comparator #(.width(5), .mode("unsigned")) comparator_1 (.a({5{1'b0}}), .b(E), .eq(Denormalized));  // open: gt, lt
  not not_1 (not_1_out, Denormalized);
  Comparator #(.width(5), .mode("unsigned")) comparator_2 (.a({5{1'b1}}), .b(E), .eq(comparator_2_eq));  // open: gt, lt
  Comparator #(.width(10)) comparator_3 (.a({10{1'b0}}), .b(M), .eq(comparator_3_eq));  // open: gt, lt
  not not_2 (not_2_out, comparator_3_eq);
  and and_1 (Infinity, comparator_2_eq, comparator_3_eq);
  not not_3 (not_3_out, comparator_2_eq);
  and and_2 (NaN, not_2_out, comparator_2_eq);
  and and_3 (Normalized, not_3_out, not_1_out);
endmodule
