// Logisim project grf.circ as structural Verilog: 1 circuit, main circuit grf
module grf (
  input  clk,
  input  reset,
  input  WE,
  input  [4:0] A1,
  input  [4:0] A2,
  input  [4:0] A3,
  input  [31:0] WD,
  output [31:0] RD1,
  output [31:0] RD2
);

  wire is2, is3, is4, is5, is6, is7, is8, is9, is10, is11, is12, is13, is14, is15, is16, is17, is18, is19,
       is20, is21, is22, is23, is24, is25, is26, is27, is28, is29, is30, is31, is32;
  wire [31:0] _1, _1_prime, _2, _2_prime, _3, _3_prime, _4, _4_prime, _5, _5_prime, _6, _6_prime, _7,
       _7_prime, _8, _8_prime, _9, _9_prime, _10, _10_prime, _11, _11_prime, _12, _12_prime, _13, _13_prime,
       _14, _14_prime, _15, _15_prime, _16, _16_prime, _17, _17_prime, _18, _18_prime, _19, _19_prime, _20,
       _20_prime, _21, _21_prime, _22, _22_prime, _23, _23_prime, _24, _24_prime, _25, _25_prime, _26,
       _26_prime, _27, _27_prime, _28, _28_prime, _29, _29_prime, _30, _30_prime, _31, _31_prime, _32,
       _32_prime;

  Comparator #(.width(5), .mode("unsigned")) comparator_1 (.a(A3), .b(5'b00001), .eq(is2));  // open: gt, lt
  Comparator #(.width(5), .mode("unsigned")) comparator_2 (.a(A3), .b(5'b00010), .eq(is3));  // open: gt, lt
  Comparator #(.width(5), .mode("unsigned")) comparator_3 (.a(A3), .b(5'b00011), .eq(is4));  // open: gt, lt
  Comparator #(.width(5), .mode("unsigned")) comparator_4 (.a(A3), .b(5'b00100), .eq(is5));  // open: gt, lt
  Comparator #(.width(5), .mode("unsigned")) comparator_5 (.a(A3), .b(5'b00101), .eq(is6));  // open: gt, lt
  Comparator #(.width(5), .mode("unsigned")) comparator_6 (.a(A3), .b(5'b00110), .eq(is7));  // open: gt, lt
  Comparator #(.width(5), .mode("unsigned")) comparator_7 (.a(A3), .b(5'b00111), .eq(is8));  // open: gt, lt
  Comparator #(.width(5), .mode("unsigned")) comparator_8 (.a(A3), .b(5'b01000), .eq(is9));  // open: gt, lt
  Comparator #(.width(5), .mode("unsigned")) comparator_9 (.a(A3), .b(5'b01001), .eq(is10));  // open: gt, lt
  Comparator #(.width(5), .mode("unsigned")) comparator_10 (.a(A3), .b(5'b01010), .eq(is11));  // open: gt, lt
  Comparator #(.width(5), .mode("unsigned")) comparator_11 (.a(A3), .b(5'b01011), .eq(is12));  // open: gt, lt
  Comparator #(.width(5), .mode("unsigned")) comparator_12 (.a(A3), .b(5'b01100), .eq(is13));  // open: gt, lt
  Comparator #(.width(5), .mode("unsigned")) comparator_13 (.a(A3), .b(5'b01101), .eq(is14));  // open: gt, lt
  Comparator #(.width(5), .mode("unsigned")) comparator_14 (.a(A3), .b(5'b01110), .eq(is15));  // open: gt, lt
  Comparator #(.width(5), .mode("unsigned")) comparator_15 (.a(A3), .b(5'b01111), .eq(is16));  // open: gt, lt
  Comparator #(.width(5), .mode("unsigned")) comparator_16 (.a(A3), .b(5'b10000), .eq(is17));  // open: gt, lt
  Comparator #(.width(5), .mode("unsigned")) comparator_17 (.a(A3), .b(5'b10001), .eq(is18));  // open: gt, lt
  Comparator #(.width(5), .mode("unsigned")) comparator_18 (.a(A3), .b(5'b10010), .eq(is19));  // open: gt, lt
  Comparator #(.width(5), .mode("unsigned")) comparator_19 (.a(A3), .b(5'b10011), .eq(is20));  // open: gt, lt
  Comparator #(.width(5), .mode("unsigned")) comparator_20 (.a(A3), .b(5'b10100), .eq(is21));  // open: gt, lt
  Comparator #(.width(5), .mode("unsigned")) comparator_21 (.a(A3), .b(5'b10101), .eq(is22));  // open: gt, lt
  Comparator #(.width(5), .mode("unsigned")) comparator_22 (.a(A3), .b(5'b10110), .eq(is23));  // open: gt, lt
  Comparator #(.width(5), .mode("unsigned")) comparator_23 (.a(A3), .b(5'b10111), .eq(is24));  // open: gt, lt
  Comparator #(.width(5), .mode("unsigned")) comparator_24 (.a(A3), .b(5'b11000), .eq(is25));  // open: gt, lt
  Comparator #(.width(5), .mode("unsigned")) comparator_25 (.a(A3), .b(5'b11001), .eq(is26));  // open: gt, lt
  Comparator #(.width(5), .mode("unsigned")) comparator_26 (.a(A3), .b(5'b11010), .eq(is27));  // open: gt, lt
  Comparator #(.width(5), .mode("unsigned")) comparator_27 (.a(A3), .b(5'b11011), .eq(is28));  // open: gt, lt
  Comparator #(.width(5), .mode("unsigned")) comparator_28 (.a(A3), .b(5'b11100), .eq(is29));  // open: gt, lt
  Comparator #(.width(5), .mode("unsigned")) comparator_29 (.a(A3), .b(5'b11101), .eq(is30));  // open: gt, lt
  Comparator #(.width(5), .mode("unsigned")) comparator_30 (.a(A3), .b(5'b11110), .eq(is31));  // open: gt, lt
  Comparator #(.width(5), .mode("unsigned")) comparator_31 (.a(A3), .b({5{1'b1}}), .eq(is32));  // open: gt, lt
  // Probe on _1
  Demultiplexer #(.select(5), .width(32)) demultiplexer_1 (
    .out0(_1), .out1(_2), .out2(_3), .out3(_4), .out4(_5), .out5(_6), .out6(_7), .out7(_8), .out8(_9),
    .out9(_10), .out10(_11), .out11(_12), .out12(_13), .out13(_14), .out14(_15), .out15(_16), .out16(_17),
    .out17(_18), .out18(_19), .out19(_20), .out20(_21), .out21(_22), .out22(_23), .out23(_24), .out24(_25),
    .out25(_26), .out26(_27), .out27(_28), .out28(_29), .out29(_30), .out30(_31), .out31(_32), .in(WD),
    .sel(A3), .en(WE));
  Register #(.width(32)) register_1 (.D({32{1'b0}}), .Q(_1_prime), .clk(clk), .clr(reset));  // open: en
  Register #(.width(32)) register_2 (.D(_5), .en(is5), .Q(_5_prime), .clk(clk), .clr(reset));
  Register #(.width(32)) register_3 (.D(_9), .en(is9), .Q(_9_prime), .clk(clk), .clr(reset));
  Register #(.width(32)) register_4 (.D(_13), .en(is13), .Q(_13_prime), .clk(clk), .clr(reset));
  Register #(.width(32)) register_5 (.D(_17), .en(is17), .Q(_17_prime), .clk(clk), .clr(reset));
  Register #(.width(32)) register_6 (.D(_21), .en(is21), .Q(_21_prime), .clk(clk), .clr(reset));
  Register #(.width(32)) register_7 (.D(_25), .en(is25), .Q(_25_prime), .clk(clk), .clr(reset));
  Register #(.width(32)) register_8 (.D(_29), .en(is29), .Q(_29_prime), .clk(clk), .clr(reset));
  Register #(.width(32)) register_9 (.D(_2), .en(is2), .Q(_2_prime), .clk(clk), .clr(reset));
  Register #(.width(32)) register_10 (.D(_6), .en(is6), .Q(_6_prime), .clk(clk), .clr(reset));
  Register #(.width(32)) register_11 (.D(_10), .en(is10), .Q(_10_prime), .clk(clk), .clr(reset));
  Register #(.width(32)) register_12 (.D(_14), .en(is14), .Q(_14_prime), .clk(clk), .clr(reset));
  Register #(.width(32)) register_13 (.D(_18), .en(is18), .Q(_18_prime), .clk(clk), .clr(reset));
  Register #(.width(32)) register_14 (.D(_22), .en(is22), .Q(_22_prime), .clk(clk), .clr(reset));
  Register #(.width(32)) register_15 (.D(_26), .en(is26), .Q(_26_prime), .clk(clk), .clr(reset));
  Register #(.width(32)) register_16 (.D(_30), .en(is30), .Q(_30_prime), .clk(clk), .clr(reset));
  Multiplexer #(.select(5), .width(32)) multiplexer_1 (
    .in0(_1_prime), .in1(_2_prime), .in2(_3_prime), .in3(_4_prime), .in4(_5_prime), .in5(_6_prime),
    .in6(_7_prime), .in7(_8_prime), .in8(_9_prime), .in9(_10_prime), .in10(_11_prime), .in11(_12_prime),
    .in12(_13_prime), .in13(_14_prime), .in14(_15_prime), .in15(_16_prime), .in16(_17_prime),
    .in17(_18_prime), .in18(_19_prime), .in19(_20_prime), .in20(_21_prime), .in21(_22_prime),
    .in22(_23_prime), .in23(_24_prime), .in24(_25_prime), .in25(_26_prime), .in26(_27_prime),
    .in27(_28_prime), .in28(_29_prime), .in29(_30_prime), .in30(_31_prime), .in31(_32_prime), .out(RD1),
    .sel(A1));  // open: en
  Register #(.width(32)) register_17 (.D(_3), .en(is3), .Q(_3_prime), .clk(clk), .clr(reset));
  Register #(.width(32)) register_18 (.D(_7), .en(is7), .Q(_7_prime), .clk(clk), .clr(reset));
  Register #(.width(32)) register_19 (.D(_11), .en(is11), .Q(_11_prime), .clk(clk), .clr(reset));
  Register #(.width(32)) register_20 (.D(_15), .en(is15), .Q(_15_prime), .clk(clk), .clr(reset));
  Register #(.width(32)) register_21 (.D(_19), .en(is19), .Q(_19_prime), .clk(clk), .clr(reset));
  Register #(.width(32)) register_22 (.D(_23), .en(is23), .Q(_23_prime), .clk(clk), .clr(reset));
  Register #(.width(32)) register_23 (.D(_27), .en(is27), .Q(_27_prime), .clk(clk), .clr(reset));
  Register #(.width(32)) register_24 (.D(_31), .en(is31), .Q(_31_prime), .clk(clk), .clr(reset));
  Register #(.width(32)) register_25 (.D(_4), .en(is4), .Q(_4_prime), .clk(clk), .clr(reset));
  Register #(.width(32)) register_26 (.D(_8), .en(is8), .Q(_8_prime), .clk(clk), .clr(reset));
  Register #(.width(32)) register_27 (.D(_12), .en(is12), .Q(_12_prime), .clk(clk), .clr(reset));
  Register #(.width(32)) register_28 (.D(_16), .en(is16), .Q(_16_prime), .clk(clk), .clr(reset));
  Register #(.width(32)) register_29 (.D(_20), .en(is20), .Q(_20_prime), .clk(clk), .clr(reset));
  Register #(.width(32)) register_30 (.D(_24), .en(is24), .Q(_24_prime), .clk(clk), .clr(reset));
  Register #(.width(32)) register_31 (.D(_28), .en(is28), .Q(_28_prime), .clk(clk), .clr(reset));
  Register #(.width(32)) register_32 (.D(_32), .en(is32), .Q(_32_prime), .clk(clk), .clr(reset));
  Multiplexer #(.select(5), .width(32)) multiplexer_2 (
    .in0(_1_prime), .in1(_2_prime), .in2(_3_prime), .in3(_4_prime), .in4(_5_prime), .in5(_6_prime),
    .in6(_7_prime), .in7(_8_prime), .in8(_9_prime), .in9(_10_prime), .in10(_11_prime), .in11(_12_prime),
    .in12(_13_prime), .in13(_14_prime), .in14(_15_prime), .in15(_16_prime), .in16(_17_prime),
    .in17(_18_prime), .in18(_19_prime), .in19(_20_prime), .in20(_21_prime), .in21(_22_prime),
    .in22(_23_prime), .in23(_24_prime), .in24(_25_prime), .in25(_26_prime), .in26(_27_prime),
    .in27(_28_prime), .in28(_29_prime), .in29(_30_prime), .in30(_31_prime), .in31(_32_prime), .out(RD2),
    .sel(A2));  // open: en

  // Other names for the same wires on the sheet: rst = reset
endmodule
