// Logisim project latch.circ as structural Verilog: 3 circuits, main circuit nor_SR_latch
module nor_SR_latch (
  input  R,
  input  S,
  output Q,
  output nQ
);

  wire or_1_out, or_2_out;

  or or_1 (or_1_out, R, nQ);
  or or_2 (or_2_out, Q, S);
  not not_1 (Q, or_1_out);
  not not_2 (nQ, or_2_out);
endmodule

module d_latch (
  input  D,
  input  E,
  output Q,
  output nQ
);

  wire and_1_out, and_2_out, not_1_out;

  not not_1 (not_1_out, D);
  and and_1 (and_1_out, not_1_out, E);
  and and_2 (and_2_out, E, D);
  nor_SR_latch NOR_SR_Latch (.R(and_1_out), .S(and_2_out), .Q(Q), .nQ(nQ));
endmodule

module d_ff (
  input  D,
  output Q,
  output nQ
);

  wire clock_1_out, Master_q, not_1_out;

  Clock clock_1 (.out(clock_1_out));
  not not_1 (not_1_out, clock_1_out);
  d_latch Master (.D(D), .E(not_1_out), .Q(Master_q));  // open: nQ
  d_latch Slave (.D(Master_q), .E(clock_1_out), .Q(Q), .nQ(nQ));
endmodule
