// Logisim project mod5.circ as structural Verilog: 3 circuits, main circuit mod5
module mod5 (
  input  In,
  output S0,
  output S1,
  output S2,
  output S3,
  output S4
);

  wire clock_1_out;
  wire [1:0] register_1_q, Trans__st1;

  trans Trans (.ST1(register_1_q[0]), .ST2(register_1_q[1]), .In(In), ._ST1(Trans__st1[0]), ._ST2(Trans__st1[1]));
  Clock clock_1 (.out(clock_1_out));
  Register #(.width(2)) register_1 (.D(Trans__st1), .Q(register_1_q), .clk(clock_1_out));  // open: en, clr
  out Out (.ST1(register_1_q[0]), .ST2(register_1_q[1]), .In(In), .S0(S0), .S1(S1), .S2(S2), .S3(S3), .S4(S4));
endmodule

module trans (
  input  ST1,
  input  ST2,
  input  In,
  output _ST1,
  output _ST2
);

  wire and_1_out, and_2_out, and_3_out, and_4_out, and_5_out, and_6_out, not_1_out, not_2_out, not_3_out,
       not_4_out, not_5_out, not_6_out, not_7_out, not_8_out;

  not not_1 (not_1_out, ST1);
  not not_2 (not_2_out, ST2);
  not not_3 (not_3_out, ST1);
  not not_4 (not_4_out, ST2);
  not not_5 (not_5_out, ST1);
  not not_6 (not_6_out, In);
  not not_7 (not_7_out, ST2);
  not not_8 (not_8_out, In);
  and and_1 (and_1_out, not_1_out, ST2);
  and and_2 (and_2_out, ST1, not_2_out);
  and and_3 (and_3_out, not_3_out, not_4_out, In);
  and and_4 (and_4_out, not_5_out, ST2, not_6_out);
  and and_5 (and_5_out, ST1, not_7_out, not_8_out);
  and and_6 (and_6_out, ST1, ST2, In);
  or or_1 (_ST1, and_1_out, and_2_out);
  or or_2 (_ST2, and_3_out, and_4_out, and_5_out, and_6_out);
endmodule

module out (
  input  ST1,
  input  ST2,
  input  In,
  output S0,
  output S1,
  output S2,
  output S3,
  output S4
);

  wire and_1_out, and_2_out, and_3_out, and_4_out, and_5_out, and_6_out, and_7_out, and_8_out, not_1_out,
       not_2_out, not_3_out, not_4_out, not_5_out, not_6_out, not_7_out, not_8_out, not_9_out, not_10_out,
       not_11_out, not_12_out;

  not not_1 (not_1_out, ST1);
  not not_2 (not_2_out, ST2);
  not not_3 (not_3_out, In);
  not not_4 (not_4_out, In);
  not not_5 (not_5_out, ST1);
  not not_6 (not_6_out, ST2);
  not not_7 (not_7_out, ST1);
  not not_8 (not_8_out, ST2);
  not not_9 (not_9_out, ST1);
  not not_10 (not_10_out, In);
  not not_11 (not_11_out, ST2);
  not not_12 (not_12_out, In);
  and and_1 (and_1_out, not_1_out, not_2_out, not_3_out);
  and and_2 (and_2_out, ST1, ST2, not_4_out);
  and and_3 (and_3_out, not_5_out, not_6_out, In);
  and and_4 (and_4_out, ST1, ST2, In);
  and and_5 (and_5_out, not_7_out, ST2, In);
  and and_6 (and_6_out, ST1, not_8_out, In);
  and and_7 (and_7_out, not_9_out, ST2, not_10_out);
  and and_8 (and_8_out, ST1, not_11_out, not_12_out);
  or or_1 (S1, and_1_out, and_2_out);
  or or_2 (S2, and_3_out, and_4_out);
  or or_3 (S3, and_5_out, and_6_out);
  or or_4 (S4, and_7_out, and_8_out);

  assign S0 = 1'b0;
endmodule
