// Logisim project navigation.circ as structural Verilog: 2 circuits, main circuit navigation
module navigation (
  input  [1:0] dir,
  input  clk,
  input  reset,
  output arrive,
  output hit
);

  wire check_1_isarrive, check_1_ishit, loc0, loc1, loc2, n_loc0, n_loc1, n_loc2;

  check check_1 (
    .dir0(dir[1]), .dir1(dir[0]), .location0(loc2), .location1(loc1), .location2(loc0), .n_location0(n_loc2),
    .n_location1(n_loc1), .n_location2(n_loc0), .isHit(check_1_ishit), .isArrive(check_1_isarrive));
  Register #(.width(3)) location (
    .D({n_loc2, n_loc1, n_loc0}), .Q({loc2, loc1, loc0}), .clk(clk), .clr(reset));  // open: en
  Register #(.width(1)) register_1 (.D(check_1_isarrive), .Q(arrive), .clk(clk), .clr(reset));  // open: en
  Register #(.width(1)) register_2 (.D(check_1_ishit), .Q(hit), .clk(clk), .clr(reset));  // open: en

  // Other names for the same wires on the sheet: rst = reset

  // Notes on the sheet:
  //   S:10
  //   N:00
  //   W:11
  //   E:01
endmodule

module check (
  input  dir0,
  input  dir1,
  input  location0,
  input  location1,
  input  location2,
  output n_location0,
  output n_location1,
  output n_location2,
  output isHit,
  output isArrive
);

  wire and_1_out, and_2_out, and_3_out, and_4_out, and_5_out, and_6_out, and_7_out, and_8_out, and_9_out,
       and_10_out, and_11_out, and_12_out, and_13_out, and_14_out, and_15_out, and_16_out, and_17_out,
       and_18_out, not_1_out, not_2_out, not_3_out, not_4_out, not_5_out, not_6_out, not_7_out, not_8_out,
       not_9_out, not_10_out, not_11_out, not_12_out, not_13_out, not_14_out, not_15_out, not_16_out,
       not_17_out, not_18_out, not_19_out, not_20_out, not_21_out, not_22_out, not_23_out, not_24_out,
       not_25_out, not_26_out, not_27_out, not_28_out, not_29_out, not_30_out, not_31_out, not_32_out,
       not_33_out;

  not not_1 (not_1_out, dir0);
  not not_2 (not_2_out, dir1);
  not not_3 (not_3_out, location2);
  not not_4 (not_4_out, dir0);
  not not_5 (not_5_out, dir1);
  not not_6 (not_6_out, dir0);
  not not_7 (not_7_out, dir1);
  not not_8 (not_8_out, location0);
  not not_9 (not_9_out, location1);
  not not_10 (not_10_out, dir0);
  not not_11 (not_11_out, dir1);
  not not_12 (not_12_out, location1);
  not not_13 (not_13_out, location2);
  not not_14 (not_14_out, dir0);
  not not_15 (not_15_out, location1);
  not not_16 (not_16_out, dir1);
  not not_17 (not_17_out, location1);
  not not_18 (not_18_out, dir0);
  not not_19 (not_19_out, location2);
  not not_20 (not_20_out, dir0);
  not not_21 (not_21_out, dir0);
  not not_22 (not_22_out, dir1);
  not not_23 (not_23_out, dir0);
  not not_24 (not_24_out, location0);
  not not_25 (not_25_out, location1);
  not not_26 (not_26_out, dir1);
  not not_27 (not_27_out, location0);
  not not_28 (not_28_out, location1);
  not not_29 (not_29_out, location2);
  not not_30 (not_30_out, dir0);
  not not_31 (not_31_out, dir1);
  not not_32 (not_32_out, location1);
  not not_33 (not_33_out, dir0);
  and and_1 (and_1_out, not_1_out, not_2_out, location1, not_3_out);
  and and_2 (and_2_out, not_4_out, not_5_out, location0);
  and and_3 (and_3_out, dir0, dir1, location0);
  and and_4 (and_4_out, not_6_out, not_7_out, not_8_out, not_9_out);
  and and_5 (and_5_out, not_10_out, dir1, location0);
  and and_6 (and_6_out, dir0, not_11_out, location0);
  and and_7 (and_7_out, dir0, dir1, not_12_out, location2);
  and and_8 (and_8_out, dir0, dir1, location1, not_13_out);
  and and_9 (and_9_out, not_14_out, not_15_out, location2);
  and and_10 (and_10_out, not_16_out, not_17_out, location2);
  and and_11 (and_11_out, not_18_out, dir1, location1, not_19_out);
  and and_12 (and_12_out, not_20_out, dir1, location0);
  and and_13 (and_13_out, not_21_out, not_22_out, location0);
  and and_14 (and_14_out, not_23_out, dir1, not_24_out, not_25_out);
  and and_15 (and_15_out, dir0, not_26_out, not_27_out, not_28_out);
  and and_16 (and_16_out, dir0, dir1, not_29_out);
  and and_17 (and_17_out, not_30_out, not_31_out, not_32_out, location2);
  and and_18 (and_18_out, not_33_out, dir1, location0);
  or or_1 (n_location0, and_1_out, and_2_out, and_3_out);
  or or_2 (n_location1, and_4_out, and_5_out, and_6_out, and_7_out, and_8_out);
  or or_3 (n_location2, and_9_out, and_10_out, and_11_out, and_12_out);
  or or_4 (isHit, and_13_out, and_14_out, and_15_out, and_16_out);
  or or_5 (isArrive, and_17_out, and_18_out);
endmodule
