// Logisim project swap.circ as structural Verilog: 3 circuits, main circuit 1bit_swap
module _1bit_swap (
  input  S,
  input  I1,
  input  I2,
  output O1,
  output O2
);

  wire and_1_out, and_2_out, and_3_out, and_4_out, not_1_out;

  not not_1 (not_1_out, S);
  and and_1 (and_1_out, not_1_out, I1);
  and and_2 (and_2_out, S, I2);
  and and_3 (and_3_out, not_1_out, I2);
  and and_4 (and_4_out, I1, S);
  or or_1 (O1, and_1_out, and_2_out);
  or or_2 (O2, and_3_out, and_4_out);
endmodule

module _4bit_swap (
  input  [3:0] I1,
  input  [3:0] I2,
  input  S,
  output [3:0] O1,
  output [3:0] O2
);

  _1bit_swap _0 (.S(S), .I1(I1[0]), .I2(I2[0]), .O1(O1[0]), .O2(O2[0]));
  _1bit_swap _1 (.S(S), .I1(I1[1]), .I2(I2[1]), .O1(O1[1]), .O2(O2[1]));
  _1bit_swap _2 (.S(S), .I1(I1[2]), .I2(I2[2]), .O1(O1[2]), .O2(O2[2]));
  _1bit_swap _3 (.S(S), .I1(I1[3]), .I2(I2[3]), .O1(O1[3]), .O2(O2[3]));

  // Other names for the same wires on the sheet: I1_0 = I1[0]; I1_1 = I1[1]; I1_2 = I1[2]; I1_3 = I1[3]; I2_0 = I2[0];
  //   I2_1 = I2[1]; I2_2 = I2[2]; I2_3 = I2[3]; O1_0 = O1[0]; O1_1 = O1[1]; O1_2 = O1[2]; O1_3 = O1[3]; O2_0 = O2[0];
  //   O2_1 = O2[1]; O2_2 = O2[2]; O2_3 = O2[3]
endmodule

module _4bit_sort (
  input  [3:0] A,
  input  [3:0] B,
  input  [3:0] C,
  input  [3:0] D,
  output [3:0] _1,
  output [3:0] _2,
  output [3:0] _3,
  output [3:0] _4
);

  wire comparator_1_gt, comparator_2_gt, comparator_3_gt, comparator_4_gt, comparator_5_gt, comparator_6_gt;
  wire [3:0] A1, A2, B1, B2, C1, C2, D1, D2;

  Comparator #(.width(4), .mode("unsigned")) comparator_1 (.a(A), .b(B), .gt(comparator_1_gt));  // open: eq, lt
  Comparator #(.width(4), .mode("unsigned")) comparator_2 (.a(A1), .b(C), .gt(comparator_2_gt));  // open: eq, lt
  Comparator #(.width(4), .mode("unsigned")) comparator_3 (.a(A2), .b(D), .gt(comparator_3_gt));  // open: eq, lt
  Comparator #(.width(4), .mode("unsigned")) comparator_4 (.a(B1), .b(C1), .gt(comparator_4_gt));  // open: eq, lt
  Comparator #(.width(4), .mode("unsigned")) comparator_5 (.a(B2), .b(D1), .gt(comparator_5_gt));  // open: eq, lt
  Comparator #(.width(4), .mode("unsigned")) comparator_6 (.a(C2), .b(D2), .gt(comparator_6_gt));  // open: eq, lt
  _4bit_swap u_4bit_swap_1 (.I1(A), .I2(B), .S(comparator_1_gt), .O1(A1), .O2(B1));
  _4bit_swap u_4bit_swap_2 (.I1(A1), .I2(C), .S(comparator_2_gt), .O1(A2), .O2(C1));
  _4bit_swap u_4bit_swap_3 (.I1(A2), .I2(D), .S(comparator_3_gt), .O1(_1), .O2(D1));
  _4bit_swap u_4bit_swap_4 (.I1(B1), .I2(C1), .S(comparator_4_gt), .O1(B2), .O2(C2));
  _4bit_swap u_4bit_swap_5 (.I1(B2), .I2(D1), .S(comparator_5_gt), .O1(_2), .O2(D2));
  _4bit_swap u_4bit_swap_6 (.I1(C2), .I2(D2), .S(comparator_6_gt), .O1(_3), .O2(_4));

  // Other names for the same wires on the sheet: A3[3:0] = _1; B3[3:0] = _2; C3[3:0] = _3; D3[3:0] = _4
endmodule
